// Logisim project FD_Group42.circ as structural Verilog: 6 circuits, main circuit main
module main (
  output [15:0] pc,
  output [15:0] r0,
  output [15:0] r1,
  output [15:0] r2,
  output [15:0] r3,
  output [15:0] r4,
  output [15:0] r5,
  output [15:0] r6,
  output [15:0] r7,
  output [15:0] r8,
  output [15:0] r9,
  output [15:0] r10,
  output [15:0] r11,
  output [15:0] r12,
  output [15:0] r13,
  output [15:0] r14,
  output [15:0] r15,
  output halt
);

  wire and_1_out, clock_1_out, control_unit_1_branch_absolute, control_unit_1_branch_relative,
       control_unit_1_immediate, control_unit_1_memld, control_unit_1_memstr, control_unit_1_readdest,
       control_unit_1_regwrite, control_unit_1_shift8, control_unit_1_storepc, error_detector_1_error,
       n16_bit_alu_1_overflow, reset_out;
  wire [1:0] immediate_1_jumpindex;
  wire [3:0] address_control_1_rd, address_control_1_rs, address_control_1_rt, control_unit_1_aluop;
  wire [15:0] adder_1_out, adder_2_out, immediate_1_imm, multiplexer_1_out, multiplexer_2_out,
       multiplexer_3_out, multiplexer_4_out, multiplexer_5_out, multiplexer_6_out, n16_bit_alu_1_result,
       ram_1_data, ram_2_data, register_file_improved_design_1_s, register_file_improved_design_1_t,
       shifter_1_out;

  Halt halt_1 (.instruction(multiplexer_1_out), .clock(clock_1_out), .reset(reset_out), .halt(halt));
  Clock clock_1 (.out(clock_1_out));
  Button reset (.out(reset_out));
  and and_1 (and_1_out, ~halt, clock_1_out);  // AND_Gate
  PC pc_1 (
    .branch_relative(control_unit_1_branch_relative), .branch_absolute(control_unit_1_branch_absolute),
    .branch_value(multiplexer_2_out), .instruction_address(pc), .reset(reset_out), .C(and_1_out));
  Adder #(.width(16)) adder_1 (.a(pc), .b(16'h1), .out(adder_1_out));  // open: cin, cout
  RAM #(.addrWidth(16), .dataWidth(16)) ram_1 (
    .addr(pc), .data(ram_1_data), .clk(and_1_out), .ld(1'b1), .clr(reset_out));  // open: sel
  Multiplexer #(.width(16), .enable("false")) multiplexer_1 (
    .in0(ram_1_data), .in1({16{1'b0}}), .out(multiplexer_1_out), .sel(error_detector_1_error));
  Error_Detector error_detector_1 (
    .Instruction(ram_1_data), .Error(error_detector_1_error), .ALU_Overflow(n16_bit_alu_1_overflow));
  Control_Unit control_unit_1 (
    .Instruction(ram_1_data), .ALUOp(control_unit_1_aluop), .MemStr(control_unit_1_memstr),
    .RegWrite(control_unit_1_regwrite), .MemLd(control_unit_1_memld), .Immediate(control_unit_1_immediate),
    .Branch_relative(control_unit_1_branch_relative), .Branch_absolute(control_unit_1_branch_absolute),
    .rd(register_file_improved_design_1_s), .StorePC(control_unit_1_storepc),
    .ReadDest(control_unit_1_readdest), .Shift8(control_unit_1_shift8));
  Register_File_Improved_Design register_file_improved_design_1 (
    .Data(multiplexer_3_out), .Reset(reset_out), .C(and_1_out), .Write(control_unit_1_regwrite),
    .T(register_file_improved_design_1_t), .rd(address_control_1_rd), .rt(address_control_1_rs), .r0(r0),
    .r1(r1), .r2(r2), .r3(r3), .r4(r4), .rs(address_control_1_rt), .r5(r5),
    .S(register_file_improved_design_1_s), .r6(r6), .r7(r7), .r8(r8), .r9(r9), .r10(r10), .r11(r11),
    .r12(r12), .r13(r13), .r14(r14), .r15(r15));
  Multiplexer #(.select(2), .width(16), .enable("false")) multiplexer_2 (
    .in0(immediate_1_imm), .in1(n16_bit_alu_1_result), .in2(immediate_1_imm), .in3(adder_2_out),
    .out(multiplexer_2_out), .sel(immediate_1_jumpindex));
  Address_Control address_control_1 (
    .StorePC(control_unit_1_storepc), .ReadDestT(control_unit_1_immediate), .Instruction(ram_1_data),
    .rd(address_control_1_rd), .rs(address_control_1_rs), .rt(address_control_1_rt),
    .ReadDestS(control_unit_1_readdest));
  Immediate immediate_1 (.in_1(ram_1_data), .imm(immediate_1_imm), .JumpIndex(immediate_1_jumpindex));
  Multiplexer #(.width(16), .enable("false")) multiplexer_3 (
    .in0(multiplexer_4_out), .in1(shifter_1_out), .out(multiplexer_3_out), .sel(control_unit_1_shift8));
  Multiplexer #(.width(16), .enable("false")) multiplexer_4 (
    .in0(multiplexer_6_out), .in1(adder_1_out), .out(multiplexer_4_out), .sel(control_unit_1_storepc));
  _16_bit_ALU u_16_bit_alu_1 (
    .ALU_code(control_unit_1_aluop), .a(register_file_improved_design_1_t), .b(multiplexer_5_out),
    .overflow(n16_bit_alu_1_overflow), .result(n16_bit_alu_1_result));
  Multiplexer #(.width(16), .enable("false")) multiplexer_5 (
    .in0(register_file_improved_design_1_s), .in1(immediate_1_imm), .out(multiplexer_5_out),
    .sel(control_unit_1_immediate));
  Shifter #(.width(16)) shifter_1 (.in(immediate_1_imm), .\dist (4'b1000), .out(shifter_1_out));
  Adder #(.width(16)) adder_2 (.a(immediate_1_imm), .b(16'h1), .out(adder_2_out));  // open: cin, cout
  Multiplexer #(.width(16), .enable("false")) multiplexer_6 (
    .in0(n16_bit_alu_1_result), .in1(ram_2_data), .out(multiplexer_6_out), .sel(control_unit_1_memld));
  RAM #(.addrWidth(16), .dataWidth(16), .bus("separate")) ram_2 (
    .addr(n16_bit_alu_1_result), .din(register_file_improved_design_1_s), .data(ram_2_data),
    .str(control_unit_1_memstr), .clk(and_1_out), .ld(control_unit_1_memld), .clr(reset_out));  // open: sel
  // Register_File_With_Outputs register_file_with_outputs_1: pin names not known

  // Notes on the sheet:
  //   current instruction
  //   clock signal
  //   reset button
  //   Instruction Memory
  //   0 j
  //   1 jr
  //   2 jal
  //   3 brnz
  //   Data RAM
endmodule

module Control_Unit (
  input  [15:0] Instruction,
  input  [15:0] rd,
  output Immediate,
  output [3:0] ALUOp,
  output MemLd,
  output MemStr,
  output RegWrite,
  output StorePC,
  output Branch_relative,
  output Branch_absolute,
  output ReadDest,
  output Shift8
);

  wire and_2_out, comparator_1_eq, eq_1_out_3, eq_4_out_3, eq_6_out_3, eq_8_out_3, eq_9_out_3, eq_10_out_3,
       not_1_out, or_2_out;
  wire [1:0] and_1_out;
  wire [3:0] multiplexer_2_out;

  Comparator #(.width(16), .mode("unsigned")) comparator_1 (
    .a(rd), .b({16{1'b0}}), .eq(comparator_1_eq));  // open: gt, lt
  EQ eq_1 (.in_1(Instruction[15:12]), .in_2(4'b0001), .out_3(eq_1_out_3));
  EQ eq_2 (.in_1(Instruction[15:12]), .in_2(4'b1010), .out_3(MemLd));
  EQ eq_3 (.in_1(Instruction[15:12]), .in_2(4'b1011), .out_3(MemStr));
  EQ eq_4 (.in_1(Instruction[15:12]), .in_2(4'b1100), .out_3(eq_4_out_3));
  EQ eq_5 (.in_1(Instruction[15:12]), .in_2(4'b1101), .out_3(Shift8));
  EQ eq_6 (.in_1(Instruction[15:12]), .in_2(4'b1110), .out_3(eq_6_out_3));
  EQ eq_7 (.in_1(Instruction[15:12]), .in_2(4'b1111), .out_3(Branch_absolute));
  EQ eq_8 (.in_1(Instruction[3:0]), .in_2(4'b1111), .out_3(eq_8_out_3));
  EQ eq_9 (.in_1(Instruction[3:0]), .in_2(4'b0100), .out_3(eq_9_out_3));
  EQ eq_10 (.in_1(Instruction[3:0]), .in_2(4'b0000), .out_3(eq_10_out_3));
  not not_1 (not_1_out, comparator_1_eq);
  and and_1 (and_1_out[0], Immediate, ~eq_4_out_3);  // AND_Gate
  Comparator #(.width(4), .mode("unsigned")) comparator_2 (
    .a(4'b1001), .b(Instruction[15:12]), .lt(Immediate));  // open: gt, eq
  or or_1 (and_1_out[1], Shift8, eq_4_out_3);
  Multiplexer #(.select(2), .width(4), .enable("false")) multiplexer_1 (
    .in0(multiplexer_2_out), .in1(4'b0100), .in2(4'b0011), .in3(4'b0011), .out(ALUOp), .sel(and_1_out));
  Multiplexer #(.width(4), .enable("false")) multiplexer_2 (
    .in0(Instruction[15:12]), .in1(Instruction[3:0]), .out(multiplexer_2_out), .sel(eq_1_out_3));
  nor nor_1 (RegWrite, eq_6_out_3, MemStr, and_2_out);
  and and_2 (and_2_out, Branch_absolute, or_2_out);
  or or_2 (or_2_out, eq_10_out_3, eq_9_out_3);
  and and_3 (StorePC, Branch_absolute, eq_8_out_3);
  and and_4 (Branch_relative, eq_6_out_3, not_1_out);
  and and_5 (ReadDest, Branch_absolute, eq_9_out_3);

  // Notes on the sheet:
  //   rs/0000
  //   rd
  //   code
  //   Unary Op
  //   lw
  //   sw
  //   ori
  //   lui
  //   brnz
  //   jump
  //   jal
  //   jr
  //   j
  //   rd not zero
  //   rt/op code/imm
endmodule

module Immediate (
  input  [15:0] in_1,
  output [1:0] JumpIndex,
  output [15:0] imm
);

  wire bitfinder_1_found, bitfinder_2_found, demultiplexer_1_out0, demultiplexer_1_out1,
       demultiplexer_1_out2, demultiplexer_1_out3, eq_1_out_3;
  wire [1:0] bitfinder_1_index, bitfinder_2_index;
  wire [2:0] eq_2_out_3;
  wire [3:0] or_1_out, subtractor_1_out;
  wire [15:0] bit_extender_1_out, bit_extender_2_out, bit_extender_3_out, bit_extender_4_out,
       bit_extender_5_out, bit_extender_6_out, multiplexer_2_out;

  Subtractor #(.width(4)) subtractor_1 (.a(in_1[15:12]), .b(4'b1010), .out(subtractor_1_out));  // open: bin, bout
  EQ eq_1 (.in_1(in_1[15:12]), .in_2(4'b1110), .out_3(eq_1_out_3));
  EQ eq_2 (.in_1(in_1[3:0]), .in_2(4'b0000), .out_3(eq_2_out_3[0]));
  EQ eq_3 (.in_1(in_1[3:0]), .in_2(4'b0100), .out_3(eq_2_out_3[1]));
  EQ eq_4 (.in_1(in_1[3:0]), .in_2(4'b1111), .out_3(eq_2_out_3[2]));
  assign bit_extender_1_out = {{8{in_1[11]}}, in_1[11:4]};  // Bit_Extender bit_extender_1
  assign bit_extender_2_out = {{12{in_1[7]}}, in_1[7:4]};  // Bit_Extender bit_extender_2
  assign bit_extender_3_out = {{8{in_1[11]}}, in_1[11:4]};  // Bit_Extender bit_extender_3
  assign bit_extender_4_out = {{8{in_1[7]}}, in_1[7:0]};  // Bit_Extender bit_extender_4
  assign bit_extender_5_out = {{8{1'b0}}, in_1[7:0]};  // Bit_Extender bit_extender_5
  assign bit_extender_6_out = {{12{in_1[3]}}, in_1[3:0]};  // Bit_Extender bit_extender_6
  Demultiplexer #(.select(3), .enable("false")) demultiplexer_1 (
    .out0(demultiplexer_1_out0), .out1(demultiplexer_1_out1), .out2(demultiplexer_1_out2),
    .out3(demultiplexer_1_out3), .out4(or_1_out[2]), .out5(or_1_out[3]), .in(1'b1),
    .sel(subtractor_1_out[2:0]));  // open: out6, out7
  Multiplexer #(.width(2), .enable("false")) multiplexer_1 (
    .in0(bitfinder_1_index), .in1(2'b11), .out(JumpIndex), .sel(eq_1_out_3));
  BitFinder #(.width(3)) bitfinder_1 (.in(eq_2_out_3), .index(bitfinder_1_index), .found(bitfinder_1_found));
  or or_1 (or_1_out[0], demultiplexer_1_out0, demultiplexer_1_out1);
  or or_2 (or_1_out[1], demultiplexer_1_out2, demultiplexer_1_out3);
  Multiplexer #(.select(2), .width(16)) multiplexer_2 (
    .in0(bit_extender_1_out), .in1(bit_extender_2_out), .in2(bit_extender_3_out), .out(multiplexer_2_out),
    .sel(bitfinder_1_index), .en(bitfinder_1_found));  // open: in3
  BitFinder #(.width(4)) bitfinder_2 (.in(or_1_out), .index(bitfinder_2_index), .found(bitfinder_2_found));
  Multiplexer #(.select(2), .width(16), .disabled(0)) multiplexer_3 (
    .in0(bit_extender_6_out), .in1(bit_extender_5_out), .in2(bit_extender_4_out), .in3(multiplexer_2_out),
    .out(imm), .sel(bitfinder_2_index), .en(bitfinder_2_found));

  // Notes on the sheet:
  //   j
  //   jr
  //   jal
  //   brnz
  //   ori / lui
  //   lw / sw
  //   0 j
  //   1 jr
  //   2 jal
  //   3 brnz
endmodule

module Address_Control (
  input  StorePC,
  input  ReadDestS,
  input  ReadDestT,
  input  [15:0] Instruction,
  output [3:0] rd,
  output [3:0] rs,
  output [3:0] rt
);

  Multiplexer #(.width(4), .enable("false")) multiplexer_1 (
    .in0(Instruction[11:8]), .in1(4'b1111), .out(rd), .sel(StorePC));
  Multiplexer #(.width(4), .enable("false")) multiplexer_2 (
    .in0(Instruction[7:4]), .in1(Instruction[11:8]), .out(rs), .sel(ReadDestS));
  Multiplexer #(.width(4), .enable("false")) multiplexer_3 (
    .in0(Instruction[3:0]), .in1(Instruction[11:8]), .out(rt), .sel(ReadDestT));

  // Notes on the sheet:
  //   rt
  //   rs
  //   rd
endmodule

module backup (
);

  Button reset ();  // open: out
endmodule

module Error_Detector (
  input  [15:0] Instruction,
  input  ALU_Overflow,
  output Error
);

  wire and_1_out, and_2_out, bitfinder_1_found, eq_1_out_3, eq_9_out_3, eq_10_out_3;
  wire [3:0] or_1_out;
  wire [6:0] eq_2_out_3;

  assign or_1_out = Instruction[3:0] | Instruction[7:4];  // OR_Gate or_1, 4 bits wide
  EQ eq_1 (.in_1(Instruction[3:0]), .in_2(4'b0000), .out_3(eq_1_out_3));
  EQ eq_2 (.in_1(Instruction[3:0]), .in_2(4'b0001), .out_3(eq_2_out_3[0]));
  EQ eq_3 (.in_1(Instruction[3:0]), .in_2(4'b1010), .out_3(eq_2_out_3[1]));
  EQ eq_4 (.in_1(Instruction[3:0]), .in_2(4'b1011), .out_3(eq_2_out_3[2]));
  EQ eq_5 (.in_1(Instruction[3:0]), .in_2(4'b1100), .out_3(eq_2_out_3[3]));
  EQ eq_6 (.in_1(Instruction[3:0]), .in_2(4'b1101), .out_3(eq_2_out_3[4]));
  EQ eq_7 (.in_1(Instruction[3:0]), .in_2(4'b1110), .out_3(eq_2_out_3[5]));
  EQ eq_8 (.in_1(Instruction[3:0]), .in_2(4'b1111), .out_3(eq_2_out_3[6]));
  EQ eq_9 (.in_1(Instruction[15:12]), .in_2(4'b0001), .out_3(eq_9_out_3));
  EQ eq_10 (.in_1(or_1_out), .in_2(4'b0000), .out_3(eq_10_out_3));
  or or_2 (Error, and_1_out, and_2_out, ALU_Overflow);
  and and_1 (and_1_out, ~eq_10_out_3, eq_1_out_3);  // AND_Gate
  BitFinder #(.width(7)) bitfinder_1 (.in(eq_2_out_3), .found(bitfinder_1_found));  // open: index
  and and_2 (and_2_out, ~bitfinder_1_found, eq_9_out_3);  // AND_Gate

  // Notes on the sheet:
  //   not
  //   inv
  //   sll
  //   srl
  //   sla
  //   sra
  //   cp
  //   Unary Op
endmodule
