// Logisim project Project1Oef3.circ as structural Verilog: 4 circuits, main circuit NAND
module NAND (
  input  in_1,
  input  in_2,
  output out_3
);

  wire and_1_out;

  not not_1 (out_3, and_1_out);
  and and_1 (and_1_out, in_1, in_2);
endmodule

module AND (
  input  in_1,
  input  in_2,
  output out_3
);

  wire nand_1_out_3, nand_2_out_3;

  NAND nand_1 (.in_1(in_1), .in_2(in_2), .out_3(nand_1_out_3));
  NAND nand_2 (.in_1(in_1), .in_2(in_2), .out_3(nand_2_out_3));
  NAND nand_3 (.in_1(nand_1_out_3), .in_2(nand_2_out_3), .out_3(out_3));
endmodule

module OR (
  input  in_1,
  input  in_2,
  output out_3
);

  wire nand_1_out_3, nand_2_out_3;

  NAND nand_1 (.in_1(in_1), .in_2(in_1), .out_3(nand_1_out_3));
  NAND nand_2 (.in_1(in_2), .in_2(in_2), .out_3(nand_2_out_3));
  NAND nand_3 (.in_1(nand_1_out_3), .in_2(nand_2_out_3), .out_3(out_3));
endmodule

module NOT (
  input  in_1,
  output out_2
);

  NAND nand_1 (.in_1(in_1), .in_2(in_1), .out_3(out_2));
endmodule
