// Logisim project Project3.circ as structural Verilog
module _16_Bit_Register (
  input  C,
  input  Write,
  input  Reset,
  input  [15:0] DI,
  output [15:0] Register
);

  D_Flip_Flop d_ff_1 (.clk(C), .D(DI[12]), .Q(Register[12]), .en(Write), .reset(Reset));  // open: Qn, preset
  D_Flip_Flop d_ff_2 (.clk(C), .D(DI[13]), .Q(Register[13]), .en(Write), .reset(Reset));  // open: Qn, preset
  D_Flip_Flop d_ff_3 (.clk(C), .D(DI[14]), .Q(Register[14]), .en(Write), .reset(Reset));  // open: Qn, preset
  D_Flip_Flop d_ff_4 (.clk(C), .D(DI[15]), .Q(Register[15]), .en(Write), .reset(Reset));  // open: Qn, preset
  D_Flip_Flop d_ff_5 (.clk(C), .D(DI[8]), .Q(Register[8]), .en(Write), .reset(Reset));  // open: Qn, preset
  D_Flip_Flop d_ff_6 (.clk(C), .D(DI[9]), .Q(Register[9]), .en(Write), .reset(Reset));  // open: Qn, preset
  D_Flip_Flop d_ff_7 (.clk(C), .D(DI[10]), .Q(Register[10]), .en(Write), .reset(Reset));  // open: Qn, preset
  D_Flip_Flop d_ff_8 (.clk(C), .D(DI[11]), .Q(Register[11]), .en(Write), .reset(Reset));  // open: Qn, preset
  D_Flip_Flop d_ff_9 (.clk(C), .D(DI[4]), .Q(Register[4]), .en(Write), .reset(Reset));  // open: Qn, preset
  D_Flip_Flop d_ff_10 (.clk(C), .D(DI[5]), .Q(Register[5]), .en(Write), .reset(Reset));  // open: Qn, preset
  D_Flip_Flop d_ff_11 (.clk(C), .D(DI[6]), .Q(Register[6]), .en(Write), .reset(Reset));  // open: Qn, preset
  D_Flip_Flop d_ff_12 (.clk(C), .D(DI[7]), .Q(Register[7]), .en(Write), .reset(Reset));  // open: Qn, preset
  D_Flip_Flop d_ff_13 (.clk(C), .D(DI[0]), .Q(Register[0]), .en(Write), .reset(Reset));  // open: Qn, preset
  D_Flip_Flop d_ff_14 (.clk(C), .D(DI[1]), .Q(Register[1]), .en(Write), .reset(Reset));  // open: Qn, preset
  D_Flip_Flop d_ff_15 (.clk(C), .D(DI[2]), .Q(Register[2]), .en(Write), .reset(Reset));  // open: Qn, preset
  D_Flip_Flop d_ff_16 (.clk(C), .D(DI[3]), .Q(Register[3]), .en(Write), .reset(Reset));  // open: Qn, preset
endmodule

module Register_File (
  input  [15:0] in_1
);

  wire undriven, undriven_2, undriven_3, undriven_4, undriven_5, undriven_6, undriven_7, undriven_8,
       undriven_9, undriven_10, undriven_11, undriven_12, undriven_13, undriven_14, undriven_15, undriven_16,
       undriven_18, undriven_19;
  wire [15:0] undriven_17;

  Decoder decoder_1 ();  // open: out0, out1, sel, en
  _16_Bit_Register u_16_bit_register_1 (
    .DI(undriven_17), .C(undriven_19), .Write(undriven), .Reset(undriven_18));  // open: Register
  _16_Bit_Register u_16_bit_register_2 (
    .DI(undriven_17), .C(undriven_19), .Write(undriven_2), .Reset(undriven_18));  // open: Register
  _16_Bit_Register u_16_bit_register_3 (
    .DI(undriven_17), .C(undriven_19), .Write(undriven_3), .Reset(undriven_18));  // open: Register
  _16_Bit_Register u_16_bit_register_4 (
    .DI(undriven_17), .C(undriven_19), .Write(undriven_4), .Reset(undriven_18));  // open: Register
  _16_Bit_Register u_16_bit_register_5 (
    .DI(undriven_17), .C(undriven_19), .Write(undriven_5), .Reset(undriven_18));  // open: Register
  _16_Bit_Register u_16_bit_register_6 (
    .DI(undriven_17), .C(undriven_19), .Write(undriven_6), .Reset(undriven_18));  // open: Register
  _16_Bit_Register u_16_bit_register_7 (
    .DI(undriven_17), .C(undriven_19), .Write(undriven_7), .Reset(undriven_18));  // open: Register
  _16_Bit_Register u_16_bit_register_8 (
    .DI(undriven_17), .C(undriven_19), .Write(undriven_8), .Reset(undriven_18));  // open: Register
  _16_Bit_Register u_16_bit_register_9 (
    .DI(undriven_17), .C(undriven_19), .Write(undriven_9), .Reset(undriven_18));  // open: Register
  _16_Bit_Register u_16_bit_register_10 (
    .DI(undriven_17), .C(undriven_19), .Write(undriven_10), .Reset(undriven_18));  // open: Register
  _16_Bit_Register u_16_bit_register_11 (
    .DI(undriven_17), .C(undriven_19), .Write(undriven_11), .Reset(undriven_18));  // open: Register
  _16_Bit_Register u_16_bit_register_12 (
    .DI(undriven_17), .C(undriven_19), .Write(undriven_12), .Reset(undriven_18));  // open: Register
  _16_Bit_Register u_16_bit_register_13 (
    .DI(undriven_17), .C(undriven_19), .Write(undriven_13), .Reset(undriven_18));  // open: Register
  _16_Bit_Register u_16_bit_register_14 (
    .DI(undriven_17), .C(undriven_19), .Write(undriven_14), .Reset(undriven_18));  // open: Register
  _16_Bit_Register u_16_bit_register_15 (
    .DI(undriven_17), .C(undriven_19), .Write(undriven_15), .Reset(undriven_18));  // open: Register
  _16_Bit_Register u_16_bit_register_16 (
    .DI(undriven_17), .C(undriven_19), .Write(undriven_16), .Reset(undriven_18));  // open: Register
endmodule
