// Logisim project ALU_Group42.circ as structural Verilog: 19 circuits, main circuit main
module main (
  output halt,
  output [8:0] counter,
  output [3:0] op,
  output [15:0] a,
  output [15:0] b,
  output [15:0] oracle,
  output [15:0] result,
  output err_oracle,
  output error,
  output ok,
  output start_delimiter
);

  wire and_1_out, and_2_out, clock_1_out, comparator_1_eq, comparator_2_eq;

  Clock clock_1 (.out(clock_1_out));
  Counter #(.width(9), .max('h1ff), .trigger("falling")) counter_1 (
    .Q(counter), .carry(halt), .clk(clock_1_out));  // open: load, D, count, clr
  RAM #(.addrWidth(12), .dataWidth(4), .bus("separate")) ram_1 (
    .addr({counter, 3'b000}), .data(op), .ld(1'b1));  // open: din, str, sel, clk, clr
  RAM #(.addrWidth(12), .dataWidth(16), .bus("separate")) ram_2 (
    .addr({counter, 3'b001}), .data(a), .ld(1'b1));  // open: din, str, sel, clk, clr
  RAM #(.addrWidth(12), .dataWidth(16), .bus("separate")) ram_3 (
    .addr({counter, 3'b010}), .data(b), .ld(1'b1));  // open: din, str, sel, clk, clr
  RAM #(.addrWidth(12), .dataWidth(16), .bus("separate")) ram_4 (
    .addr({counter, 3'b011}), .data(oracle), .ld(1'b1));  // open: din, str, sel, clk, clr
  RAM #(.addrWidth(12), .dataWidth(1), .bus("separate")) ram_5 (
    .addr({counter, 3'b100}), .data(err_oracle), .ld(1'b1));  // open: din, str, sel, clk, clr
  RAM #(.addrWidth(12), .dataWidth(1), .bus("separate")) ram_6 (
    .addr({counter, 3'b101}), .data(start_delimiter), .ld(1'b1));  // open: din, str, sel, clk, clr
  // _16_bit_ALU 16_bit_alu_1: pin names not known; wires that end beside it: a, b, op, op, result, error
  Comparator #(.width(1), .mode("unsigned")) comparator_1 (
    .a(error), .b(err_oracle), .eq(comparator_1_eq));  // open: gt, lt
  Comparator #(.width(16)) comparator_2 (.a(result), .b(oracle), .eq(comparator_2_eq));  // open: gt, lt
  and and_1 (and_1_out, comparator_1_eq, error);
  and and_2 (and_2_out, comparator_2_eq, comparator_1_eq, ~error);  // AND_Gate
  or or_1 (ok, and_1_out, and_2_out);

  // Notes on the sheet:
  //   You must complete the circuit '16-bit ALU' instead.
  //   DO NOT EDIT THIS CIRCUIT!
endmodule

module _16_bit_ALU (
  input  [3:0] ALU_code,
  input  [15:0] a,
  input  [15:0] b,
  output [15:0] result,
  output overflow
);

  wire add_1_overflow, inv_1_out_3, sla_1_overflow, sub_1_overflow;
  wire [3:0] not_2_out;
  wire [15:0] add_1_sum, and_1_out_3, equals_1_out_3, gt_1_out_3, inv_1_out_2, lt_1_out_3, nequals_1_out_3,
       noop_1_out_2, not_1_out_2, or_1_out_3, sla_1_out_2, sll_1_out_2, sra_1_out_2, srl_1_out_2,
       sub_1_out_4, zero_1_out_1;

  // Probe on a
  // Probe on b
  ZERO zero_1 (.out_1(zero_1_out_1));
  NOT not_1 (.in_1(a), .out_2(not_1_out_2));
  AND and_1 (.in_1(a), .in_2(b), .out_3(and_1_out_3));
  OR or_1 (.in_1(a), .in_2(b), .out_3(or_1_out_3));
  ADD add_1 (.in_1(a), .in_2(b), .sum(add_1_sum), .Overflow(add_1_overflow));
  SUB sub_1 (.in_1(a), .in_2(b), .out_4(sub_1_out_4), .Overflow(sub_1_overflow));  // open: C4
  LT lt_1 (.a(a), .b(b), .out_3(lt_1_out_3));
  GT gt_1 (.a(a), .b(b), .out_3(gt_1_out_3));
  EQUALS equals_1 (.in_1(a), .in_2(b), .out_3(equals_1_out_3));
  NEQUALS nequals_1 (.in_1(a), .in_2(b), .out_3(nequals_1_out_3));
  INV inv_1 (.in_1(a), .out_2(inv_1_out_2), .out_3(inv_1_out_3));
  SLL sll_1 (.in_1(a), .out_2(sll_1_out_2));
  SRL srl_1 (.in_1(a), .out_2(srl_1_out_2));
  SLA sla_1 (.Overflow(sla_1_overflow), .in_1(a), .out_2(sla_1_out_2));
  SRA sra_1 (.in_1(a), .out_2(sra_1_out_2));
  NOOP noop_1 (.in_1(a), .out_2(noop_1_out_2));
  Multiplexer #(.select(4)) multiplexer_1 (
    .in0(1'b0), .in1(1'b0), .in2(sla_1_overflow), .in3(1'b0), .in4(1'b0), .in5(inv_1_out_3), .in6(1'b0),
    .in7(1'b0), .in8(1'b0), .in9(1'b0), .in10(sub_1_overflow), .in11(add_1_overflow), .in12(1'b0),
    .in13(1'b0), .in14(1'b0), .in15(1'b0), .out(overflow), .sel(not_2_out));  // open: en
  assign not_2_out = ~ALU_code;  // NOT_Gate not_2, 4 bits wide
  Multiplexer #(.select(4), .width(16)) multiplexer_2 (
    .in0(zero_1_out_1), .in1(not_1_out_2), .in2(and_1_out_3), .in3(or_1_out_3), .in4(add_1_sum),
    .in5(sub_1_out_4), .in6(lt_1_out_3), .in7(gt_1_out_3), .in8(equals_1_out_3), .in9(nequals_1_out_3),
    .in10(inv_1_out_2), .in11(sll_1_out_2), .in12(srl_1_out_2), .in13(sla_1_out_2), .in14(sra_1_out_2),
    .in15(noop_1_out_2), .out(result), .sel(ALU_code));  // open: en
  // Probe on result

  // Other names for the same wires on the sheet: code[3:0] = ALU_code

  // Notes on the sheet:
  //   This circuit is used as a block in the main circuit, and its layout must remain unchanged. The circuit called "main" should be the main circuit of this file.
  //   Do not change the circuit appearance.
  //   DO NOT CHANGE THE INPUTS AND OUTPUTS OF THIS CIRCUIT!
  //   Do not add/remove inputs or outputs. Do not even change their location or orientation.
endmodule

module LT (
  input  [15:0] a,
  input  [15:0] b,
  output [15:0] out_3
);

  // Probe on a
  // Probe on b
  GT gt_1 (.a(b), .b(a), .out_3(out_3));
endmodule

module SUB (
  input  [15:0] in_1,
  input  [15:0] in_2,
  output C4,
  output [15:0] out_4,
  output Overflow
);

  wire inv_1_out_3, n16_bit_cla_optimised_1_overflow;
  wire [15:0] inv_1_out_2;

  // Probe on in_1
  INV inv_1 (.in_1(in_2), .out_2(inv_1_out_2), .out_3(inv_1_out_3));
  _16_Bit_CLA_Optimised u_16_bit_cla_optimised_1 (
    .in_1(in_1), .in_2(inv_1_out_2), .out_5(out_4), .Overflow(n16_bit_cla_optimised_1_overflow), .C4(C4));
  xor xor_1 (Overflow, n16_bit_cla_optimised_1_overflow, inv_1_out_3);
  // Probe on out_4
endmodule

module ADD (
  input  [15:0] in_1,
  input  [15:0] in_2,
  output [15:0] sum,
  output Overflow
);

  _16_Bit_CLA_Optimised u_16_bit_cla_optimised_1 (
    .in_1(in_1), .in_2(in_2), .out_5(sum), .Overflow(Overflow));  // open: C4
endmodule

module ZERO (
  output [15:0] out_1
);


  assign out_1 = {16{1'b0}};
endmodule

module NOT (
  input  [15:0] in_1,
  output [15:0] out_2
);

  assign out_2 = ~in_1;  // NOT_Gate not_1, 16 bits wide
endmodule

module AND (
  input  [15:0] in_1,
  input  [15:0] in_2,
  output [15:0] out_3
);

  assign out_3 = in_1 & in_2;  // AND_Gate and_1, 16 bits wide
endmodule

module OR (
  input  [15:0] in_1,
  input  [15:0] in_2,
  output [15:0] out_3
);

  assign out_3 = in_1 | in_2;  // OR_Gate or_1, 16 bits wide
endmodule

module GT (
  input  [15:0] a,
  input  [15:0] b,
  output [15:0] out_3
);

  wire multiplexer_1_out, multiplexer_2_out;
  wire [15:0] abs_1_out_2, abs_2_out_2, equals_1_out_3, sub_1_out_4;

  ABS abs_1 (.in_1(a), .out_2(abs_1_out_2));
  ABS abs_2 (.in_1(b), .out_2(abs_2_out_2));
  EQUALS equals_1 (.in_1(a), .in_2(b), .out_3(equals_1_out_3));
  SUB sub_1 (.in_1(abs_1_out_2), .in_2(abs_2_out_2), .out_4(sub_1_out_4));  // open: Overflow, C4
  Multiplexer multiplexer_1 (
    .in0(multiplexer_2_out), .in1(1'b0), .out(multiplexer_1_out), .sel(equals_1_out_3[0]));  // open: en
  Multiplexer #(.select(3)) multiplexer_2 (
    .in0(1'b1), .in1(1'b0), .in2(1'b1), .in3(1'b1), .in4(1'b0), .in5(1'b0), .in6(1'b0), .in7(1'b1),
    .out(multiplexer_2_out), .sel({a[15], b[15], sub_1_out_4[15]}));  // open: en
  assign out_3 = {{15{1'b0}}, multiplexer_1_out};  // Bit_Extender bit_extender_1
endmodule

module EQUALS (
  input  [15:0] in_1,
  input  [15:0] in_2,
  output [15:0] out_3
);

  wire and_1_out;
  wire [15:0] xnor_1_out;

  assign xnor_1_out = ~(in_1 ^ in_2);  // XNOR_Gate xnor_1, 16 bits wide
  and and_1 (and_1_out, xnor_1_out[0], xnor_1_out[1], xnor_1_out[2], xnor_1_out[3], xnor_1_out[4], xnor_1_out[5], xnor_1_out[6], xnor_1_out[7], xnor_1_out[8], xnor_1_out[9], xnor_1_out[10], xnor_1_out[11], xnor_1_out[12], xnor_1_out[13], xnor_1_out[14], xnor_1_out[15]);
  assign out_3 = {{15{1'b0}}, and_1_out};  // Bit_Extender bit_extender_1
endmodule

module NEQUALS (
  input  [15:0] in_1,
  input  [15:0] in_2,
  output [15:0] out_3
);

  wire not_1_out;
  wire [15:0] equals_1_out_3;

  EQUALS equals_1 (.in_1(in_1), .in_2(in_2), .out_3(equals_1_out_3));
  not not_1 (not_1_out, equals_1_out_3[0]);
  assign out_3 = {{15{1'b0}}, not_1_out};  // Bit_Extender bit_extender_1
endmodule

module INV (
  input  [15:0] in_1,
  output [15:0] out_2,
  output out_3
);

  wire [15:0] not_1_out;

  assign not_1_out = ~in_1;  // NOT_Gate not_1, 16 bits wide
  // Probe on in_1
  _16_Bit_CLA_Optimised u_16_bit_cla_optimised_1 (
    .in_1(16'h1), .in_2(not_1_out), .out_5(out_2), .Overflow(out_3));  // open: C4
  // Probe on out_2
endmodule

module SLL (
  input  [15:0] in_1,
  output [15:0] out_2
);


  assign out_2 = {in_1[14:0], 1'b0};
endmodule

module SRL (
  input  [15:0] in_1,
  output [15:0] out_2
);


  assign out_2 = {1'b0, in_1[15:1]};
endmodule

module SLA (
  input  [15:0] in_1,
  output [15:0] out_2,
  output Overflow
);

  xor xor_1 (Overflow, in_1[14], in_1[15]);

  assign out_2 = {in_1[14:0], 1'b0};
endmodule

module SRA (
  input  [15:0] in_1,
  output [15:0] out_2
);


  assign out_2 = {{2{in_1[15]}}, in_1[14:1]};
endmodule

module NOOP (
  input  [15:0] in_1,
  output [15:0] out_2
);


  assign out_2 = in_1;
endmodule

module ABS (
  input  [15:0] in_1,
  output [15:0] out_2
);

  wire [15:0] inv_1_out_2;

  INV inv_1 (.in_1(in_1), .out_2(inv_1_out_2));  // open: out_3
  Multiplexer #(.width(16)) multiplexer_1 (.in0(in_1), .in1(inv_1_out_2), .out(out_2), .sel(in_1[15]));  // open: en
endmodule
