// Logisim project Project1Oef4.circ as structural Verilog: 1 circuit, main circuit Truthtable
module Truthtable (
  input  A,
  input  B,
  input  C,
  output X,
  output Y
);

  wire and_1_out, and_2_out, and_3_out, or_1_out, or_2_out, or_3_out;

  and and_1 (and_1_out, A, C);
  and and_2 (and_2_out, B, C);
  or or_1 (or_1_out, B, and_2_out);
  and and_3 (and_3_out, and_2_out, B);
  or or_2 (or_2_out, and_1_out, or_1_out);
  or or_3 (or_3_out, and_1_out, and_3_out);
  not not_1 (X, or_2_out);
  not not_2 (Y, or_3_out);
endmodule
