// Logisim project Project4.circ as structural Verilog
module _16_Bit_Register (
  input  C,
  input  Write,
  input  Reset,
  input  [15:0] D,
  output [15:0] Register
);

  D_Flip_Flop #(.trigger("falling")) d_ff_1 (
    .clk(C), .D(D[12]), .Q(Register[12]), .en(Write), .reset(Reset));  // open: Qn, preset
  D_Flip_Flop #(.trigger("falling")) d_ff_2 (
    .clk(C), .D(D[13]), .Q(Register[13]), .en(Write), .reset(Reset));  // open: Qn, preset
  D_Flip_Flop #(.trigger("falling")) d_ff_3 (
    .clk(C), .D(D[14]), .Q(Register[14]), .en(Write), .reset(Reset));  // open: Qn, preset
  D_Flip_Flop #(.trigger("falling")) d_ff_4 (
    .clk(C), .D(D[15]), .Q(Register[15]), .en(Write), .reset(Reset));  // open: Qn, preset
  D_Flip_Flop #(.trigger("falling")) d_ff_5 (
    .clk(C), .D(D[8]), .Q(Register[8]), .en(Write), .reset(Reset));  // open: Qn, preset
  D_Flip_Flop #(.trigger("falling")) d_ff_6 (
    .clk(C), .D(D[9]), .Q(Register[9]), .en(Write), .reset(Reset));  // open: Qn, preset
  D_Flip_Flop #(.trigger("falling")) d_ff_7 (
    .clk(C), .D(D[10]), .Q(Register[10]), .en(Write), .reset(Reset));  // open: Qn, preset
  D_Flip_Flop #(.trigger("falling")) d_ff_8 (
    .clk(C), .D(D[11]), .Q(Register[11]), .en(Write), .reset(Reset));  // open: Qn, preset
  D_Flip_Flop #(.trigger("falling")) d_ff_9 (
    .clk(C), .D(D[4]), .Q(Register[4]), .en(Write), .reset(Reset));  // open: Qn, preset
  D_Flip_Flop #(.trigger("falling")) d_ff_10 (
    .clk(C), .D(D[5]), .Q(Register[5]), .en(Write), .reset(Reset));  // open: Qn, preset
  D_Flip_Flop #(.trigger("falling")) d_ff_11 (
    .clk(C), .D(D[6]), .Q(Register[6]), .en(Write), .reset(Reset));  // open: Qn, preset
  D_Flip_Flop #(.trigger("falling")) d_ff_12 (
    .clk(C), .D(D[7]), .Q(Register[7]), .en(Write), .reset(Reset));  // open: Qn, preset
  D_Flip_Flop #(.trigger("falling")) d_ff_13 (
    .clk(C), .D(D[0]), .Q(Register[0]), .en(Write), .reset(Reset));  // open: Qn, preset
  D_Flip_Flop #(.trigger("falling")) d_ff_14 (
    .clk(C), .D(D[1]), .Q(Register[1]), .en(Write), .reset(Reset));  // open: Qn, preset
  D_Flip_Flop #(.trigger("falling")) d_ff_15 (
    .clk(C), .D(D[2]), .Q(Register[2]), .en(Write), .reset(Reset));  // open: Qn, preset
  D_Flip_Flop #(.trigger("falling")) d_ff_16 (
    .clk(C), .D(D[3]), .Q(Register[3]), .en(Write), .reset(Reset));  // open: Qn, preset
endmodule

module Register_File (
  input  [15:0] Data,
  input  Reset,
  input  C,
  input  Write,
  input  [3:0] rd,
  input  [3:0] rt,
  input  [3:0] rs,
  output [15:0] T,
  output [15:0] S
);

  wire decoder_1_out1, decoder_1_out2, decoder_1_out3, decoder_1_out4, decoder_1_out5, decoder_1_out6,
       decoder_1_out7, decoder_1_out8, decoder_1_out9, decoder_1_out10, decoder_1_out11, decoder_1_out12,
       decoder_1_out13, decoder_1_out14, decoder_1_out15;
  wire [15:0] n16_bit_register_1_register, n16_bit_register_2_register, n16_bit_register_3_register,
       n16_bit_register_4_register, n16_bit_register_5_register, n16_bit_register_6_register,
       n16_bit_register_7_register, n16_bit_register_8_register, n16_bit_register_9_register,
       n16_bit_register_10_register, n16_bit_register_11_register, n16_bit_register_12_register,
       n16_bit_register_13_register, n16_bit_register_14_register, n16_bit_register_15_register,
       n16_bit_register_16_register;

  Decoder #(.select(4), .disabled(0)) decoder_1 (
    .out1(decoder_1_out1), .out2(decoder_1_out2), .out3(decoder_1_out3), .out4(decoder_1_out4),
    .out5(decoder_1_out5), .out6(decoder_1_out6), .out7(decoder_1_out7), .out8(decoder_1_out8),
    .out9(decoder_1_out9), .out10(decoder_1_out10), .out11(decoder_1_out11), .out12(decoder_1_out12),
    .out13(decoder_1_out13), .out14(decoder_1_out14), .out15(decoder_1_out15), .sel(rd), .en(Write));  // open: out0
  _16_Bit_Register u_16_bit_register_1 (
    .D({16{1'b0}}), .Register(n16_bit_register_1_register), .C(C), .Write(1'b0), .Reset(Reset));
  _16_Bit_Register u_16_bit_register_2 (
    .D(Data), .Register(n16_bit_register_2_register), .C(C), .Write(decoder_1_out1), .Reset(Reset));
  _16_Bit_Register u_16_bit_register_3 (
    .D(Data), .Register(n16_bit_register_3_register), .C(C), .Write(decoder_1_out2), .Reset(Reset));
  _16_Bit_Register u_16_bit_register_4 (
    .D(Data), .Register(n16_bit_register_4_register), .C(C), .Write(decoder_1_out3), .Reset(Reset));
  _16_Bit_Register u_16_bit_register_5 (
    .D(Data), .Register(n16_bit_register_5_register), .C(C), .Write(decoder_1_out4), .Reset(Reset));
  _16_Bit_Register u_16_bit_register_6 (
    .D(Data), .Register(n16_bit_register_6_register), .C(C), .Write(decoder_1_out5), .Reset(Reset));
  _16_Bit_Register u_16_bit_register_7 (
    .D(Data), .Register(n16_bit_register_7_register), .C(C), .Write(decoder_1_out6), .Reset(Reset));
  _16_Bit_Register u_16_bit_register_8 (
    .D(Data), .Register(n16_bit_register_8_register), .C(C), .Write(decoder_1_out7), .Reset(Reset));
  _16_Bit_Register u_16_bit_register_9 (
    .D(Data), .Register(n16_bit_register_9_register), .C(C), .Write(decoder_1_out8), .Reset(Reset));
  _16_Bit_Register u_16_bit_register_10 (
    .D(Data), .Register(n16_bit_register_10_register), .C(C), .Write(decoder_1_out9), .Reset(Reset));
  _16_Bit_Register u_16_bit_register_11 (
    .D(Data), .Register(n16_bit_register_11_register), .C(C), .Write(decoder_1_out10), .Reset(Reset));
  _16_Bit_Register u_16_bit_register_12 (
    .D(Data), .Register(n16_bit_register_12_register), .C(C), .Write(decoder_1_out11), .Reset(Reset));
  _16_Bit_Register u_16_bit_register_13 (
    .D(Data), .Register(n16_bit_register_13_register), .C(C), .Write(decoder_1_out12), .Reset(Reset));
  _16_Bit_Register u_16_bit_register_14 (
    .D(Data), .Register(n16_bit_register_14_register), .C(C), .Write(decoder_1_out13), .Reset(Reset));
  _16_Bit_Register u_16_bit_register_15 (
    .D(Data), .Register(n16_bit_register_15_register), .C(C), .Write(decoder_1_out14), .Reset(Reset));
  _16_Bit_Register u_16_bit_register_16 (
    .D(Data), .Register(n16_bit_register_16_register), .C(C), .Write(decoder_1_out15), .Reset(Reset));
  Multiplexer #(.select(4), .width(16), .disabled(0), .enable("false")) multiplexer_1 (
    .in0(n16_bit_register_1_register), .in1(n16_bit_register_2_register), .in2(n16_bit_register_3_register),
    .in3(n16_bit_register_4_register), .in4(n16_bit_register_5_register), .in5(n16_bit_register_6_register),
    .in6(n16_bit_register_7_register), .in7(n16_bit_register_8_register), .in8(n16_bit_register_9_register),
    .in9(n16_bit_register_10_register), .in10(n16_bit_register_11_register),
    .in11(n16_bit_register_12_register), .in12(n16_bit_register_13_register),
    .in13(n16_bit_register_14_register), .in14(n16_bit_register_15_register),
    .in15(n16_bit_register_16_register), .out(T), .sel(rt));
  Multiplexer #(.select(4), .width(16), .disabled(0), .enable("false")) multiplexer_2 (
    .in0(n16_bit_register_1_register), .in1(n16_bit_register_2_register), .in2(n16_bit_register_3_register),
    .in3(n16_bit_register_4_register), .in4(n16_bit_register_5_register), .in5(n16_bit_register_6_register),
    .in6(n16_bit_register_7_register), .in7(n16_bit_register_8_register), .in8(n16_bit_register_9_register),
    .in9(n16_bit_register_10_register), .in10(n16_bit_register_11_register),
    .in11(n16_bit_register_12_register), .in12(n16_bit_register_13_register),
    .in13(n16_bit_register_14_register), .in14(n16_bit_register_15_register),
    .in15(n16_bit_register_16_register), .out(S), .sel(rs));

  // Notes on the sheet:
  //   Write
  //   Read
endmodule

module Traffic_light (
);

  wire and_1_out, and_2_out, and_3_out, clock_1_out, comparator_1_gt, comparator_2_gt, comparator_3_gt,
       comparator_4_gt, comparator_5_gt, nor_1_out, nor_2_out;
  wire [15:0] counter_1_out_3;

  Clock clock_1 (.out(clock_1_out));
  Counter counter_1 (.C(clock_1_out), .D(16'h1c), .out_3(counter_1_out_3));
  // Probe on counter_1_out_3
  Comparator #(.width(16)) comparator_1 (.a(counter_1_out_3), .b(16'hb), .gt(comparator_1_gt));  // open: eq, lt
  and and_1 (and_1_out, ~comparator_1_gt, comparator_2_gt);  // AND_Gate
  Comparator #(.width(16)) comparator_2 (.a(counter_1_out_3), .b(16'h7), .gt(comparator_2_gt));  // open: eq, lt
  Comparator #(.width(16)) comparator_3 (.a(counter_1_out_3), .b(16'h19), .gt(comparator_3_gt));  // open: eq, lt
  Comparator #(.width(16)) comparator_4 (.a(counter_1_out_3), .b(16'h15), .gt(comparator_4_gt));  // open: eq, lt
  Comparator #(.width(16)) comparator_5 (.a(counter_1_out_3), .b(16'hd), .gt(comparator_5_gt));  // open: eq, lt
  LED led_1 (.in(comparator_1_gt));
  LED led_2 (.in(and_1_out));
  nor nor_1 (nor_1_out, comparator_1_gt, and_1_out);
  LED led_3 (.in(nor_1_out));
  nor nor_2 (nor_2_out, and_2_out, and_3_out);
  LED led_4 (.in(nor_2_out));
  and and_2 (and_2_out, ~comparator_3_gt, comparator_4_gt);  // AND_Gate
  LED led_5 (.in(and_2_out));
  LED led_6 (.in(and_3_out));
  and and_3 (and_3_out, ~comparator_3_gt, ~comparator_4_gt, comparator_5_gt);  // AND_Gate
endmodule

module Counter (
  input  C,
  input  [15:0] D,
  output [15:0] out_3
);

  wire comparator_1_lt, not_1_out;
  wire [15:0] n16_bit_cla_optimised_1_out_4;

  not not_1 (not_1_out, comparator_1_lt);
  _16_Bit_Register u_16_bit_register_1 (
    .D(n16_bit_cla_optimised_1_out_4), .Register(out_3), .C(C), .Write(comparator_1_lt), .Reset(not_1_out));
  _16_Bit_CLA_Optimised u_16_bit_cla_optimised_1 (
    .in_1(16'h1), .in_2(out_3), .out_4(n16_bit_cla_optimised_1_out_4));  // open: Overflow
  Comparator #(.width(16)) comparator_1 (.a(out_3), .b(D), .lt(comparator_1_lt));  // open: gt, eq
endmodule

module Stack (
  input  Push,
  input  Pop,
  input  [15:0] Data,
  input  C,
  input  reset,
  output Error,
  output [15:0] Top_of_Stack
);

  wire and_1_out, and_2_out, comparator_1_eq, or_2_out, or_3_out, or_4_out, subtractor_1_bout;
  wire [15:0] adder_1_out, multiplexer_1_out, multiplexer_2_out, multiplexer_3_out,
       n16_bit_register_1_register, ram_1_data, subtractor_1_out, subtractor_2_out;

  or or_1 (Error, and_1_out, and_2_out);
  or or_2 (or_2_out, Push, Pop);
  and and_1 (and_1_out, Push, Pop);
  and and_2 (and_2_out, subtractor_1_bout, Pop);
  Multiplexer #(.width(16), .enable("false")) multiplexer_1 (
    .in0(Data), .in1({16{1'b0}}), .out(multiplexer_1_out), .sel(Pop));
  Adder #(.width(16)) adder_1 (.a(n16_bit_register_1_register), .b(16'h1), .out(adder_1_out));  // open: cin, cout
  Subtractor #(.width(16)) subtractor_1 (
    .a(n16_bit_register_1_register), .b(16'h1), .out(subtractor_1_out), .bout(subtractor_1_bout));  // open: bin
  Multiplexer #(.select(2), .width(16)) multiplexer_2 (
    .in0({16{1'b0}}), .in1(adder_1_out), .in2(subtractor_1_out), .in3({16{1'b0}}), .out(multiplexer_2_out),
    .sel({Pop, Push}));  // open: en
  _16_Bit_Register u_16_bit_register_1 (
    .D(multiplexer_2_out), .Register(n16_bit_register_1_register), .C(C), .Write(or_2_out), .Reset(reset));
  Comparator #(.width(16)) comparator_1 (
    .a(n16_bit_register_1_register), .b({16{1'b0}}), .eq(comparator_1_eq));  // open: gt, lt
  or or_3 (or_3_out, comparator_1_eq, Push);
  Subtractor #(.width(16)) subtractor_2 (
    .a(n16_bit_register_1_register), .b(16'h1), .out(subtractor_2_out));  // open: bin, bout
  Multiplexer #(.width(16), .enable("false")) multiplexer_3 (
    .in0(subtractor_2_out), .in1(n16_bit_register_1_register), .out(multiplexer_3_out), .sel(or_3_out));
  RAM #(.addrWidth(16), .dataWidth(16), .bus("separate")) ram_1 (
    .addr(multiplexer_3_out), .din(multiplexer_1_out), .data(ram_1_data), .str(or_2_out), .clk(C), .ld(1'b1),
    .clr(reset));  // open: sel
  or or_4 (or_4_out, comparator_1_eq, or_2_out);
  Multiplexer #(.width(16), .enable("false")) multiplexer_4 (
    .in0(ram_1_data), .in1({16{1'b0}}), .out(Top_of_Stack), .sel(or_4_out));
endmodule
