// Logisim project SD_Group42.circ as structural Verilog: 8 circuits, main circuit main
module main (
  output [15:0] pc,
  output [15:0] r0,
  output [15:0] r1,
  output [15:0] r2,
  output [15:0] r3,
  output [15:0] r4,
  output [15:0] r5,
  output [15:0] r6,
  output [15:0] r7,
  output [15:0] r8,
  output [15:0] r9,
  output [15:0] r10,
  output [15:0] r11,
  output [15:0] r12,
  output [15:0] r13,
  output [15:0] r14,
  output [15:0] r15,
  output halt
);

  wire and_1_out, clock_1_out, not_1_out, or_1_out, reset_out;
  wire [2:0] comparator_1_eq;
  wire [3:0] multiplexer_1_out, multiplexer_3_out, multiplexer_4_out, ram_1_data, ram_1_data_3;
  wire [11:4] ram_1_data_2;
  wire [15:0] bit_extender_1_out, multiplexer_2_out, multiplexer_5_out, n16_bit_alu_1_result, ram_2_data,
       register_file_with_outputs_1_s, register_file_with_outputs_1_t;

  Halt halt_1 (
    .instruction({ram_1_data_3, ram_1_data_2, ram_1_data}), .clock(clock_1_out), .reset(reset_out),
    .halt(halt));
  Clock clock_1 (.out(clock_1_out));
  Button reset (.out(reset_out));
  and and_1 (and_1_out, ~halt, clock_1_out);  // AND_Gate
  PC pc_1 (
    .branch_relative(1'b0), .branch_absolute(1'b0), .branch_value({16{1'b0}}), .instruction_address(pc),
    .reset(reset_out), .C(and_1_out));
  RAM #(.addrWidth(16), .dataWidth(16)) ram_1 (
    .addr(pc), .data({ram_1_data_3, ram_1_data_2, ram_1_data}), .clk(and_1_out), .ld(1'b1), .clr(reset_out));  // open: sel
  Multiplexer #(.width(4), .enable("false")) multiplexer_1 (
    .in0(ram_1_data), .in1(ram_1_data_2[11:8]), .out(multiplexer_1_out), .sel(or_1_out));
  Comparator #(.width(4)) comparator_1 (.a(ram_1_data_3), .b(4'b0001), .eq(comparator_1_eq[0]));  // open: gt, lt
  Comparator #(.width(4)) comparator_2 (.a(ram_1_data_3), .b(4'b1010), .eq(comparator_1_eq[1]));  // open: gt, lt
  Comparator #(.width(4)) comparator_3 (.a(ram_1_data_3), .b(4'b1011), .eq(comparator_1_eq[2]));  // open: gt, lt
  Multiplexer #(.width(16), .enable("false")) multiplexer_2 (
    .in0(n16_bit_alu_1_result), .in1(ram_2_data), .out(multiplexer_2_out), .sel(comparator_1_eq[1]));
  // NOR_Gate nor_1 has open pins: in0=comparator_1_eq[0], in1=comparator_1_eq[1], in2=comparator_1_eq[2], out=open
  not not_1 (not_1_out, comparator_1_eq[2]);
  Register_File_With_Outputs register_file_with_outputs_1 (
    .Data(multiplexer_2_out), .Reset(reset_out), .C(and_1_out), .Write(not_1_out), .rd(ram_1_data_2[11:8]),
    .rt(multiplexer_1_out), .rs(ram_1_data_2[7:4]), .r0(r0), .r1(r1), .r2(r2), .r3(r3), .r4(r4), .r5(r5),
    .r6(r6), .r7(r7), .r8(r8), .r9(r9), .r10(r10), .r11(r11), .r12(r12), .r13(r13), .r14(r14), .r15(r15),
    .T(register_file_with_outputs_1_t), .S(register_file_with_outputs_1_s));
  assign bit_extender_1_out = {{12{ram_1_data[3]}}, ram_1_data};  // Bit_Extender bit_extender_1
  or or_1 (or_1_out, comparator_1_eq[2], comparator_1_eq[1]);
  Multiplexer #(.width(4), .enable("false")) multiplexer_3 (
    .in0(ram_1_data_3), .in1(ram_1_data), .out(multiplexer_3_out), .sel(comparator_1_eq[0]));
  Multiplexer #(.width(4), .enable("false")) multiplexer_4 (
    .in0(multiplexer_3_out), .in1(4'b0100), .out(multiplexer_4_out), .sel(or_1_out));
  Multiplexer #(.width(16), .enable("false")) multiplexer_5 (
    .in0(register_file_with_outputs_1_t), .in1(bit_extender_1_out), .out(multiplexer_5_out), .sel(or_1_out));
  _16_bit_ALU u_16_bit_alu_1 (
    .ALU_code(multiplexer_4_out), .a(register_file_with_outputs_1_s), .b(multiplexer_5_out),
    .result(n16_bit_alu_1_result));  // open: overflow
  RAM #(.addrWidth(16), .dataWidth(16), .bus("separate")) ram_2 (
    .addr(n16_bit_alu_1_result), .din(register_file_with_outputs_1_t), .data(ram_2_data),
    .str(comparator_1_eq[2]), .clk(and_1_out), .ld(comparator_1_eq[1]), .clr(reset_out));  // open: sel

  // Notes on the sheet:
  //   current instruction
  //   rt/op code/imm
  //   rs/0000
  //   rd
  //   code
  //   clock signal
  //   reset button
  //   Instruction Memory
  //   Unary Op
  //   lw
  //   sw
  //   Binary Op
  //   ALU code
  //   DO NOT CHANGE THE INPUTS AND OUTPUTS OF THIS CIRCUIT! Do not add/remove inputs or outputs. Do not even change their location or orientation.
  //   Data RAM
endmodule

module Halt (
  input  [15:0] instruction,
  input  clock,
  input  reset,
  output halt
);

  wire and_1_out, comparator_1_eq, comparator_2_gt, counter_1_carry, or_1_out, or_2_out;
  wire [11:0] counter_1_q;

  Comparator #(.width(16), .mode("unsigned")) comparator_1 (
    .a(instruction), .b({16{1'b0}}), .eq(comparator_1_eq));  // open: gt, lt
  Counter #(.width(12), .max('hfff), .trigger("falling")) counter_1 (
    .Q(counter_1_q), .carry(counter_1_carry), .clk(clock), .clr(reset));  // open: load, D, count
  or or_1 (or_1_out, comparator_1_eq, counter_1_carry);
  Comparator #(.width(12), .mode("unsigned")) comparator_2 (
    .a(counter_1_q), .b({12{1'b0}}), .gt(comparator_2_gt));  // open: eq, lt
  or or_2 (or_2_out, halt, and_1_out);
  and and_1 (and_1_out, or_1_out, comparator_2_gt);
  Register #(.width(1)) register_1 (.D(or_2_out), .Q(halt), .clk(clock), .clr(reset));  // open: en

  // Notes on the sheet:
  //   halt becomes and stays asserted if the instruction is 0000 (not in the first clock cycle) or the end of the counter is reached (2^12)
endmodule

module PC (
  input  [15:0] branch_value,
  input  branch_relative,
  input  branch_absolute,
  input  reset,
  input  C,
  output [15:0] instruction_address
);

  wire xor_1_out;
  wire [15:0] add_1_sum, add_2_sum, multiplexer_1_out, multiplexer_2_out;

  ADD add_1 (.in_1(instruction_address), .in_2(branch_value), .sum(add_1_sum));  // open: Overflow
  Multiplexer #(.width(16), .enable("false")) multiplexer_1 (
    .in0(add_1_sum), .in1(branch_value), .out(multiplexer_1_out), .sel(branch_absolute));
  xor xor_1 (xor_1_out, branch_relative, branch_absolute);
  ADD add_2 (.in_1(instruction_address), .in_2(16'h1), .sum(add_2_sum));  // open: Overflow
  Multiplexer #(.width(16), .enable("false")) multiplexer_2 (
    .in0(add_2_sum), .in1(multiplexer_1_out), .out(multiplexer_2_out), .sel(xor_1_out));
  _16_Bit_Register u_16_bit_register_1 (
    .D(multiplexer_2_out), .Register(instruction_address), .C(C), .Write(1'b1), .Reset(reset));
endmodule

module Register_File_With_Outputs (
  input  [15:0] Data,
  input  Reset,
  input  C,
  input  Write,
  input  [3:0] rd,
  input  [3:0] rt,
  input  [3:0] rs,
  output [15:0] T,
  output [15:0] r0,
  output [15:0] r1,
  output [15:0] r2,
  output [15:0] r3,
  output [15:0] r4,
  output [15:0] r5,
  output [15:0] S,
  output [15:0] r6,
  output [15:0] r7,
  output [15:0] r8,
  output [15:0] r9,
  output [15:0] r10,
  output [15:0] r11,
  output [15:0] r12,
  output [15:0] r13,
  output [15:0] r14,
  output [15:0] r15
);

  wire decoder_1_out1, decoder_1_out2, decoder_1_out3, decoder_1_out4, decoder_1_out5, decoder_1_out6,
       decoder_1_out7, decoder_1_out8, decoder_1_out9, decoder_1_out10, decoder_1_out11, decoder_1_out12,
       decoder_1_out13, decoder_1_out14, decoder_1_out15;

  Decoder #(.select(4), .disabled(0)) decoder_1 (
    .out1(decoder_1_out1), .out2(decoder_1_out2), .out3(decoder_1_out3), .out4(decoder_1_out4),
    .out5(decoder_1_out5), .out6(decoder_1_out6), .out7(decoder_1_out7), .out8(decoder_1_out8),
    .out9(decoder_1_out9), .out10(decoder_1_out10), .out11(decoder_1_out11), .out12(decoder_1_out12),
    .out13(decoder_1_out13), .out14(decoder_1_out14), .out15(decoder_1_out15), .sel(rd), .en(Write));  // open: out0
  _16_Bit_Register u_16_bit_register_1 (.D({16{1'b0}}), .Register(r0), .C(C), .Write(1'b0), .Reset(Reset));
  _16_Bit_Register u_16_bit_register_2 (.D(Data), .Register(r1), .C(C), .Write(decoder_1_out1), .Reset(Reset));
  _16_Bit_Register u_16_bit_register_3 (.D(Data), .Register(r2), .C(C), .Write(decoder_1_out2), .Reset(Reset));
  _16_Bit_Register u_16_bit_register_4 (.D(Data), .Register(r3), .C(C), .Write(decoder_1_out3), .Reset(Reset));
  _16_Bit_Register u_16_bit_register_5 (.D(Data), .Register(r4), .C(C), .Write(decoder_1_out4), .Reset(Reset));
  _16_Bit_Register u_16_bit_register_6 (.D(Data), .Register(r5), .C(C), .Write(decoder_1_out5), .Reset(Reset));
  _16_Bit_Register u_16_bit_register_7 (.D(Data), .Register(r6), .C(C), .Write(decoder_1_out6), .Reset(Reset));
  _16_Bit_Register u_16_bit_register_8 (.D(Data), .Register(r7), .C(C), .Write(decoder_1_out7), .Reset(Reset));
  _16_Bit_Register u_16_bit_register_9 (.D(Data), .Register(r8), .C(C), .Write(decoder_1_out8), .Reset(Reset));
  _16_Bit_Register u_16_bit_register_10 (.D(Data), .Register(r9), .C(C), .Write(decoder_1_out9), .Reset(Reset));
  _16_Bit_Register u_16_bit_register_11 (.D(Data), .Register(r10), .C(C), .Write(decoder_1_out10), .Reset(Reset));
  _16_Bit_Register u_16_bit_register_12 (.D(Data), .Register(r11), .C(C), .Write(decoder_1_out11), .Reset(Reset));
  _16_Bit_Register u_16_bit_register_13 (.D(Data), .Register(r12), .C(C), .Write(decoder_1_out12), .Reset(Reset));
  _16_Bit_Register u_16_bit_register_14 (.D(Data), .Register(r13), .C(C), .Write(decoder_1_out13), .Reset(Reset));
  _16_Bit_Register u_16_bit_register_15 (.D(Data), .Register(r14), .C(C), .Write(decoder_1_out14), .Reset(Reset));
  _16_Bit_Register u_16_bit_register_16 (.D(Data), .Register(r15), .C(C), .Write(decoder_1_out15), .Reset(Reset));
  Multiplexer #(.select(4), .width(16), .disabled(0), .enable("false")) multiplexer_1 (
    .in0(r0), .in1(r1), .in2(r2), .in3(r3), .in4(r4), .in5(r5), .in6(r6), .in7(r7), .in8(r8), .in9(r9),
    .in10(r10), .in11(r11), .in12(r12), .in13(r13), .in14(r14), .in15(r15), .out(T), .sel(rt));
  Multiplexer #(.select(4), .width(16), .disabled(0), .enable("false")) multiplexer_2 (
    .in0(r0), .in1(r1), .in2(r2), .in3(r3), .in4(r4), .in5(r5), .in6(r6), .in7(r7), .in8(r8), .in9(r9),
    .in10(r10), .in11(r11), .in12(r12), .in13(r13), .in14(r14), .in15(r15), .out(S), .sel(rs));

  // Notes on the sheet:
  //   Write
  //   Read
endmodule

module temp (
  output [15:0] r0,
  output [15:0] r1,
  output [15:0] r2,
  output [15:0] r3,
  output [15:0] r4,
  output [15:0] r5,
  output [15:0] r6,
  output [15:0] r7,
  output [15:0] pc,
  output [15:0] r8,
  output [15:0] r9,
  output [15:0] r10,
  output [15:0] r11,
  output [15:0] r12,
  output [15:0] r13,
  output [15:0] r14,
  output [15:0] r15,
  output halt
);

  wire and_1_out, clock_1_out, eq_1_out_3, eq_2_out_3, eq_3_out_3, or_1_out,
       register_file_improved_design_1_p13, reset_out;
  wire [3:0] multiplexer_4_out, multiplexer_5_out, register_file_improved_design_1_p20;
  wire [15:0] bit_extend_1_out_2, multiplexer_3_out, n16_bit_alu_1_result, ram_1_data, ram_2_data,
       register_file_improved_design_1_p23, register_file_improved_design_1_p24,
       register_file_improved_design_1_p25;

  Halt halt_1 (.instruction(ram_1_data), .clock(clock_1_out), .reset(reset_out), .halt(halt));
  Clock clock_1 (.out(clock_1_out));
  Button reset (.out(reset_out));
  and and_1 (and_1_out, ~halt, clock_1_out);  // AND_Gate
  PC pc_1 (
    .branch_relative(1'b0), .branch_absolute(1'b0), .branch_value({16{1'b0}}), .instruction_address(pc));  // open: reset, C
  RAM #(.addrWidth(16), .dataWidth(16)) ram_1 (
    .addr(pc), .data(ram_1_data), .clk(and_1_out), .ld(1'b1), .clr(reset_out));  // open: sel
  EQ eq_1 (.in_1(ram_1_data[15:12]), .in_2(4'b0001), .out_3(eq_1_out_3));
  EQ eq_2 (.in_1(ram_1_data[15:12]), .in_2(4'b1010), .out_3(eq_2_out_3));
  EQ eq_3 (.in_1(ram_1_data[15:12]), .in_2(4'b1011), .out_3(eq_3_out_3));
  // Register_File_Improved_Design register_file_improved_design_1: pin names not known; wires that end beside it: r0, r1, r2, r3, r4, r5, r6, r7, r8, reset_out, and_1_out, r9, register_file_improved_design_1_p13, r10, ram_1_data[11:8], r11, ram_1_data[7:4], r12, r13, register_file_improved_design_1_p20, r14, r15, register_file_improved_design_1_p23, register_file_improved_design_1_p24, register_file_improved_design_1_p25
  not not_1 (register_file_improved_design_1_p13, eq_3_out_3);
  Multiplexer #(.width(4), .enable("false")) multiplexer_1 (
    .in0(ram_1_data[3:0]), .in1(ram_1_data[11:8]), .out(register_file_improved_design_1_p20), .sel(or_1_out));
  Bit_Extend bit_extend_1 (.in_1(ram_1_data[3:0]), .out_2(bit_extend_1_out_2));
  or or_1 (or_1_out, eq_2_out_3, eq_3_out_3);
  Multiplexer #(.width(16), .enable("false")) multiplexer_2 (
    .in0(ram_2_data), .in1(n16_bit_alu_1_result), .out(register_file_improved_design_1_p23), .sel(eq_2_out_3));
  _16_bit_ALU u_16_bit_alu_1 (
    .ALU_code(multiplexer_4_out), .a(register_file_improved_design_1_p24), .b(multiplexer_3_out),
    .result(n16_bit_alu_1_result));  // open: overflow
  Multiplexer #(.width(16), .enable("false")) multiplexer_3 (
    .in0(register_file_improved_design_1_p25), .in1(bit_extend_1_out_2), .out(multiplexer_3_out));  // open: sel
  Multiplexer #(.width(4), .enable("false")) multiplexer_4 (
    .in0(multiplexer_5_out), .in1(4'b0100), .out(multiplexer_4_out), .sel(or_1_out));
  Multiplexer #(.width(4), .enable("false")) multiplexer_5 (
    .in0(ram_1_data[3:0]), .in1(ram_1_data[15:12]), .out(multiplexer_5_out), .sel(eq_1_out_3));
  RAM #(.addrWidth(16), .dataWidth(16), .bus("separate")) ram_2 (
    .addr(n16_bit_alu_1_result), .data(ram_2_data), .str(eq_3_out_3), .clk(and_1_out), .ld(eq_2_out_3),
    .clr(reset_out));  // open: din, sel
  Register_File_With_Outputs register_file_with_outputs_1 ();  // open: Data, Reset, C, Write, rd, rt, rs, r0, r1, r2, r3, r4, r5, r6, r7, r8, r9, r10, r11, r12, r13, r14, r15, T, S

  // Notes on the sheet:
  //   current instruction
  //   clock signal
  //   reset button
  //   Instruction Memory
  //   rs/0000
  //   rd
  //   code
  //   Unary Op
  //   lw
  //   sw
  //   rt/op code/imm
  //   Data RAM
endmodule

module Register_File_Improved_Design (
  input  [15:0] Data,
  input  Reset,
  input  C,
  input  Write,
  input  [3:0] rd,
  input  [3:0] rt,
  input  [3:0] rs,
  output [15:0] T,
  output [15:0] r0,
  output [15:0] r1,
  output [15:0] r2,
  output [15:0] r3,
  output [15:0] r4,
  output [15:0] r5,
  output [15:0] S,
  output [15:0] r6,
  output [15:0] r7,
  output [15:0] r8,
  output [15:0] r9,
  output [15:0] r10,
  output [15:0] r11,
  output [15:0] r12,
  output [15:0] r13,
  output [15:0] r14,
  output [15:0] r15
);

  wire decoder_1_out1, decoder_1_out2, decoder_1_out3, decoder_1_out4, decoder_1_out5, decoder_1_out6,
       decoder_1_out7, decoder_1_out8, decoder_1_out9, decoder_1_out10, decoder_1_out11, decoder_1_out12,
       decoder_1_out13, decoder_1_out14, decoder_1_out15;

  Decoder #(.select(4), .disabled(0)) decoder_1 (
    .out1(decoder_1_out1), .out2(decoder_1_out2), .out3(decoder_1_out3), .out4(decoder_1_out4),
    .out5(decoder_1_out5), .out6(decoder_1_out6), .out7(decoder_1_out7), .out8(decoder_1_out8),
    .out9(decoder_1_out9), .out10(decoder_1_out10), .out11(decoder_1_out11), .out12(decoder_1_out12),
    .out13(decoder_1_out13), .out14(decoder_1_out14), .out15(decoder_1_out15), .sel(rd), .en(Write));  // open: out0
  _16_Bit_Register u_16_bit_register_1 (.D({16{1'b0}}), .Register(r0), .C(C), .Write(1'b0), .Reset(Reset));
  _16_Bit_Register u_16_bit_register_2 (.D(Data), .Register(r1), .C(C), .Write(decoder_1_out1), .Reset(Reset));
  _16_Bit_Register u_16_bit_register_3 (.D(Data), .Register(r2), .C(C), .Write(decoder_1_out2), .Reset(Reset));
  _16_Bit_Register u_16_bit_register_4 (.D(Data), .Register(r3), .C(C), .Write(decoder_1_out3), .Reset(Reset));
  _16_Bit_Register u_16_bit_register_5 (.D(Data), .Register(r4), .C(C), .Write(decoder_1_out4), .Reset(Reset));
  _16_Bit_Register u_16_bit_register_6 (.D(Data), .Register(r5), .C(C), .Write(decoder_1_out5), .Reset(Reset));
  _16_Bit_Register u_16_bit_register_7 (.D(Data), .Register(r6), .C(C), .Write(decoder_1_out6), .Reset(Reset));
  _16_Bit_Register u_16_bit_register_8 (.D(Data), .Register(r7), .C(C), .Write(decoder_1_out7), .Reset(Reset));
  _16_Bit_Register u_16_bit_register_9 (.D(Data), .Register(r8), .C(C), .Write(decoder_1_out8), .Reset(Reset));
  _16_Bit_Register u_16_bit_register_10 (.D(Data), .Register(r9), .C(C), .Write(decoder_1_out9), .Reset(Reset));
  _16_Bit_Register u_16_bit_register_11 (.D(Data), .Register(r10), .C(C), .Write(decoder_1_out10), .Reset(Reset));
  _16_Bit_Register u_16_bit_register_12 (.D(Data), .Register(r11), .C(C), .Write(decoder_1_out11), .Reset(Reset));
  _16_Bit_Register u_16_bit_register_13 (.D(Data), .Register(r12), .C(C), .Write(decoder_1_out12), .Reset(Reset));
  _16_Bit_Register u_16_bit_register_14 (.D(Data), .Register(r13), .C(C), .Write(decoder_1_out13), .Reset(Reset));
  _16_Bit_Register u_16_bit_register_15 (.D(Data), .Register(r14), .C(C), .Write(decoder_1_out14), .Reset(Reset));
  _16_Bit_Register u_16_bit_register_16 (.D(Data), .Register(r15), .C(C), .Write(decoder_1_out15), .Reset(Reset));
  Multiplexer #(.select(4), .width(16), .disabled(0), .enable("false")) multiplexer_1 (
    .in0(r0), .in1(r1), .in2(r2), .in3(r3), .in4(r4), .in5(r5), .in6(r6), .in7(r7), .in8(r8), .in9(r9),
    .in10(r10), .in11(r11), .in12(r12), .in13(r13), .in14(r14), .in15(r15), .out(T), .sel(rt));
  Multiplexer #(.select(4), .width(16), .disabled(0), .enable("false")) multiplexer_2 (
    .in0(r0), .in1(r1), .in2(r2), .in3(r3), .in4(r4), .in5(r5), .in6(r6), .in7(r7), .in8(r8), .in9(r9),
    .in10(r10), .in11(r11), .in12(r12), .in13(r13), .in14(r14), .in15(r15), .out(S), .sel(rs));

  // Notes on the sheet:
  //   Write
  //   Read
endmodule

module EQ (
  input  [3:0] in_1,
  input  [3:0] in_2,
  output out_3
);

  Comparator #(.width(4)) comparator_1 (.a(in_1), .b(in_2), .eq(out_3));  // open: gt, lt
endmodule

module Bit_Extend (
  input  [3:0] in_1,
  output [15:0] out_2
);

  assign out_2 = {{12{1'b0}}, in_1};  // Bit_Extender bit_extender_1
endmodule
