// Logisim project Project1Oef5.circ as structural Verilog: 2 circuits, main circuit 7BitDecoder
module _7BitDecoder (
  input  [2:0] in_1,
  output A,
  output B,
  output C,
  output D,
  output E,
  output F,
  output G
);

  wire _0_out, _1_out, _2_out, _4_out, _5_out, _6_out, _7_out;

  and _0 (_0_out, ~in_1[0], ~in_1[1], ~in_1[2]);  // AND_Gate
  and _1 (_1_out, in_1[0], ~in_1[1], ~in_1[2]);  // AND_Gate
  and _2 (_2_out, ~in_1[0], in_1[1], ~in_1[2]);  // AND_Gate
  // AND_Gate _3 has open pins: in0=in_1[0], in1=in_1[1], in2=in_1[2], out=open
  and _7 (_7_out, in_1[0], in_1[1], in_1[2]);
  and _6 (_6_out, ~in_1[0], in_1[1], in_1[2]);  // AND_Gate
  and _5 (_5_out, in_1[0], ~in_1[1], in_1[2]);  // AND_Gate
  and _4 (_4_out, ~in_1[0], ~in_1[1], in_1[2]);  // AND_Gate
  nor nor_1 (A, _1_out, _4_out);
  nor nor_2 (B, _5_out, _6_out);
  not not_1 (C, _2_out);
  nor nor_3 (D, _1_out, _4_out, _7_out);
  or or_1 (E, _0_out, _2_out, _6_out);
  or or_2 (F, _0_out, _4_out, _5_out, _6_out);
  nor nor_4 (G, _0_out, _1_out, _7_out);
endmodule

module _7BitDisplay (
  input  [2:0] in_1
);

  wire n7bitdecoder_1_a, n7bitdecoder_1_b, n7bitdecoder_1_c, n7bitdecoder_1_d, n7bitdecoder_1_e,
       n7bitdecoder_1_f, n7bitdecoder_1_g;

  _7BitDecoder u_7bitdecoder_1 (
    .A(n7bitdecoder_1_a), .B(n7bitdecoder_1_b), .C(n7bitdecoder_1_c), .D(n7bitdecoder_1_d),
    .E(n7bitdecoder_1_e), .F(n7bitdecoder_1_f), .G(n7bitdecoder_1_g), .in_1(in_1));
  _7_Segment_Display u_7_segment_display_1 (
    .g(n7bitdecoder_1_g), .f(n7bitdecoder_1_f), .a(n7bitdecoder_1_a), .b(n7bitdecoder_1_b),
    .e(n7bitdecoder_1_e), .d(n7bitdecoder_1_d), .c(n7bitdecoder_1_c));  // open: dp
endmodule
