// Logisim project oefening_1.circ as structural Verilog: 1 circuit, main circuit main
module main (
  input  CarryIn,
  input  a,
  input  b,
  output Sum,
  output CarryOut
);

  wire and_1_out, and_2_out, and_3_out, and_4_out, and_5_out, and_6_out, and_7_out, and_8_out;

  and and_1 (and_1_out, a, ~b, CarryIn);  // AND_Gate
  and and_2 (and_2_out, ~a, b, CarryIn);  // AND_Gate
  or or_1 (CarryOut, and_2_out, and_1_out, and_4_out, and_3_out);
  and and_3 (and_3_out, a, b, CarryIn);
  and and_4 (and_4_out, a, b, ~CarryIn);  // AND_Gate
  and and_5 (and_5_out, ~a, ~b, CarryIn);  // AND_Gate
  and and_6 (and_6_out, ~a, b, ~CarryIn);  // AND_Gate
  and and_7 (and_7_out, a, ~b, ~CarryIn);  // AND_Gate
  and and_8 (and_8_out, a, b, CarryIn);
  or or_2 (Sum, and_5_out, and_6_out, and_7_out, and_8_out);
endmodule
