// Logisim project oefening_2.circ as structural Verilog: 2 circuits, main circuit 16-bit ripple adder
module _16_bit_ripple_adder (
  input  in_1,
  input  [15:0] in_2,
  input  [15:0] in_3,
  output [15:0] out_4,
  output out_5,
  output Overflow
);

  wire n1_bit_adder_1_carryout, n1_bit_adder_2_carryout, n1_bit_adder_3_carryout, n1_bit_adder_4_carryout,
       n1_bit_adder_5_carryout, n1_bit_adder_6_carryout, n1_bit_adder_7_carryout, n1_bit_adder_8_carryout,
       n1_bit_adder_9_carryout, n1_bit_adder_10_carryout, n1_bit_adder_11_carryout, n1_bit_adder_12_carryout,
       n1_bit_adder_13_carryout, n1_bit_adder_14_carryout, n1_bit_adder_15_carryout;

  _1_bit_adder u_1_bit_adder_1 (
    .a(in_2[0]), .b(in_3[0]), .CarryIn(in_1), .CarryOut(n1_bit_adder_1_carryout), .Sum(out_4[0]));
  _1_bit_adder u_1_bit_adder_2 (
    .a(in_2[2]), .b(in_3[2]), .CarryIn(n1_bit_adder_3_carryout), .CarryOut(n1_bit_adder_2_carryout),
    .Sum(out_4[2]));
  _1_bit_adder u_1_bit_adder_3 (
    .a(in_2[1]), .b(in_3[1]), .CarryIn(n1_bit_adder_1_carryout), .CarryOut(n1_bit_adder_3_carryout),
    .Sum(out_4[1]));
  _1_bit_adder u_1_bit_adder_4 (
    .a(in_2[3]), .b(in_3[3]), .CarryIn(n1_bit_adder_2_carryout), .CarryOut(n1_bit_adder_4_carryout),
    .Sum(out_4[3]));
  _1_bit_adder u_1_bit_adder_5 (
    .a(in_2[4]), .b(in_3[4]), .CarryIn(n1_bit_adder_4_carryout), .CarryOut(n1_bit_adder_5_carryout),
    .Sum(out_4[4]));
  _1_bit_adder u_1_bit_adder_6 (
    .a(in_2[6]), .b(in_3[6]), .CarryIn(n1_bit_adder_7_carryout), .CarryOut(n1_bit_adder_6_carryout),
    .Sum(out_4[6]));
  _1_bit_adder u_1_bit_adder_7 (
    .a(in_2[5]), .b(in_3[5]), .CarryIn(n1_bit_adder_5_carryout), .CarryOut(n1_bit_adder_7_carryout),
    .Sum(out_4[5]));
  _1_bit_adder u_1_bit_adder_8 (
    .a(in_2[7]), .b(in_3[7]), .CarryIn(n1_bit_adder_6_carryout), .CarryOut(n1_bit_adder_8_carryout),
    .Sum(out_4[7]));
  _1_bit_adder u_1_bit_adder_9 (
    .a(in_2[10]), .b(in_3[10]), .CarryIn(n1_bit_adder_11_carryout), .CarryOut(n1_bit_adder_9_carryout),
    .Sum(out_4[10]));
  _1_bit_adder u_1_bit_adder_10 (
    .a(in_2[8]), .b(in_3[8]), .CarryIn(n1_bit_adder_8_carryout), .CarryOut(n1_bit_adder_10_carryout),
    .Sum(out_4[8]));
  _1_bit_adder u_1_bit_adder_11 (
    .a(in_2[9]), .b(in_3[9]), .CarryIn(n1_bit_adder_10_carryout), .CarryOut(n1_bit_adder_11_carryout),
    .Sum(out_4[9]));
  _1_bit_adder u_1_bit_adder_12 (
    .a(in_2[12]), .b(in_3[12]), .CarryIn(n1_bit_adder_13_carryout), .CarryOut(n1_bit_adder_12_carryout),
    .Sum(out_4[12]));
  _1_bit_adder u_1_bit_adder_13 (
    .a(in_2[11]), .b(in_3[11]), .CarryIn(n1_bit_adder_9_carryout), .CarryOut(n1_bit_adder_13_carryout),
    .Sum(out_4[11]));
  _1_bit_adder u_1_bit_adder_14 (
    .a(in_2[14]), .b(in_3[14]), .CarryIn(n1_bit_adder_15_carryout), .CarryOut(n1_bit_adder_14_carryout),
    .Sum(out_4[14]));
  _1_bit_adder u_1_bit_adder_15 (
    .a(in_2[13]), .b(in_3[13]), .CarryIn(n1_bit_adder_12_carryout), .CarryOut(n1_bit_adder_15_carryout),
    .Sum(out_4[13]));
  _1_bit_adder u_1_bit_adder_16 (
    .a(in_2[15]), .b(in_3[15]), .CarryIn(n1_bit_adder_14_carryout), .CarryOut(out_5), .Sum(out_4[15]));
  xor xor_1 (Overflow, out_5, n1_bit_adder_14_carryout);
endmodule

module _1_bit_adder (
  input  CarryIn,
  input  a,
  input  b,
  output Sum,
  output CarryOut
);

  wire and_1_out, and_2_out, and_3_out, and_4_out, and_5_out, and_6_out, and_7_out, and_8_out;

  and and_1 (and_1_out, a, ~b, CarryIn);  // AND_Gate
  and and_2 (and_2_out, ~a, b, CarryIn);  // AND_Gate
  or or_1 (CarryOut, and_2_out, and_1_out, and_3_out, and_4_out);
  and and_3 (and_3_out, a, b, ~CarryIn);  // AND_Gate
  and and_4 (and_4_out, a, b, CarryIn);
  and and_5 (and_5_out, ~a, ~b, CarryIn);  // AND_Gate
  and and_6 (and_6_out, ~a, b, ~CarryIn);  // AND_Gate
  and and_7 (and_7_out, a, ~b, ~CarryIn);  // AND_Gate
  and and_8 (and_8_out, a, b, CarryIn);
  or or_2 (Sum, and_5_out, and_6_out, and_7_out, and_8_out);
endmodule
