// Logisim project Project2.circ as structural Verilog
module _1_Bit_Full_Adder (
  input  CI,
  input  A,
  input  B,
  output Sum,
  output CO
);

  wire and_1_out, and_2_out, xor_1_out;

  and and_1 (and_1_out, B, A);
  or or_1 (CO, and_1_out, and_2_out);
  xor xor_1 (xor_1_out, A, B);
  and and_2 (and_2_out, CI, xor_1_out);
  xor xor_2 (Sum, CI, xor_1_out);
endmodule

module _16_Bit_Full_Adder (
  input  [15:0] in_1,
  input  [15:0] in_2,
  output [15:0] out_3,
  output Overflow
);

  wire n1_bit_full_adder_2_co, n1_bit_full_adder_3_co, n1_bit_full_adder_4_co, n1_bit_full_adder_5_co,
       n1_bit_full_adder_6_co, n1_bit_full_adder_7_co, n1_bit_full_adder_8_co, n1_bit_full_adder_9_co,
       n1_bit_full_adder_10_co, n1_bit_full_adder_11_co, n1_bit_full_adder_12_co, n1_bit_full_adder_13_co,
       n1_bit_full_adder_14_co, n1_bit_full_adder_15_co, n1_bit_full_adder_16_co;

  _1_Bit_Full_Adder u_1_bit_full_adder_1 (
    .A(in_1[15]), .B(in_2[15]), .Sum(out_3[15]), .CI(n1_bit_full_adder_3_co), .CO(Overflow));
  // Probe on in_1
  _1_Bit_Full_Adder u_1_bit_full_adder_2 (
    .A(in_1[13]), .B(in_2[13]), .Sum(out_3[13]), .CI(n1_bit_full_adder_4_co), .CO(n1_bit_full_adder_2_co));
  _1_Bit_Full_Adder u_1_bit_full_adder_3 (
    .A(in_1[14]), .B(in_2[14]), .Sum(out_3[14]), .CI(n1_bit_full_adder_2_co), .CO(n1_bit_full_adder_3_co));
  _1_Bit_Full_Adder u_1_bit_full_adder_4 (
    .A(in_1[12]), .B(in_2[12]), .Sum(out_3[12]), .CI(n1_bit_full_adder_5_co), .CO(n1_bit_full_adder_4_co));
  // Probe on in_2
  _1_Bit_Full_Adder u_1_bit_full_adder_5 (
    .A(in_1[11]), .B(in_2[11]), .Sum(out_3[11]), .CI(n1_bit_full_adder_7_co), .CO(n1_bit_full_adder_5_co));
  // Probe on out_3
  _1_Bit_Full_Adder u_1_bit_full_adder_6 (
    .A(in_1[9]), .B(in_2[9]), .Sum(out_3[9]), .CI(n1_bit_full_adder_8_co), .CO(n1_bit_full_adder_6_co));
  _1_Bit_Full_Adder u_1_bit_full_adder_7 (
    .A(in_1[10]), .B(in_2[10]), .Sum(out_3[10]), .CI(n1_bit_full_adder_6_co), .CO(n1_bit_full_adder_7_co));
  _1_Bit_Full_Adder u_1_bit_full_adder_8 (
    .A(in_1[8]), .B(in_2[8]), .Sum(out_3[8]), .CI(n1_bit_full_adder_9_co), .CO(n1_bit_full_adder_8_co));
  _1_Bit_Full_Adder u_1_bit_full_adder_9 (
    .A(in_1[7]), .B(in_2[7]), .Sum(out_3[7]), .CI(n1_bit_full_adder_11_co), .CO(n1_bit_full_adder_9_co));
  _1_Bit_Full_Adder u_1_bit_full_adder_10 (
    .A(in_1[5]), .B(in_2[5]), .Sum(out_3[5]), .CI(n1_bit_full_adder_12_co), .CO(n1_bit_full_adder_10_co));
  _1_Bit_Full_Adder u_1_bit_full_adder_11 (
    .A(in_1[6]), .B(in_2[6]), .Sum(out_3[6]), .CI(n1_bit_full_adder_10_co), .CO(n1_bit_full_adder_11_co));
  _1_Bit_Full_Adder u_1_bit_full_adder_12 (
    .A(in_1[4]), .B(in_2[4]), .Sum(out_3[4]), .CI(n1_bit_full_adder_13_co), .CO(n1_bit_full_adder_12_co));
  _1_Bit_Full_Adder u_1_bit_full_adder_13 (
    .A(in_1[3]), .B(in_2[3]), .Sum(out_3[3]), .CI(n1_bit_full_adder_14_co), .CO(n1_bit_full_adder_13_co));
  _1_Bit_Full_Adder u_1_bit_full_adder_14 (
    .A(in_1[2]), .B(in_2[2]), .Sum(out_3[2]), .CI(n1_bit_full_adder_15_co), .CO(n1_bit_full_adder_14_co));
  _1_Bit_Full_Adder u_1_bit_full_adder_15 (
    .A(in_1[1]), .B(in_2[1]), .Sum(out_3[1]), .CI(n1_bit_full_adder_16_co), .CO(n1_bit_full_adder_15_co));
  _1_Bit_Full_Adder u_1_bit_full_adder_16 (
    .A(in_1[0]), .B(in_2[0]), .Sum(out_3[0]), .CI(1'b0), .CO(n1_bit_full_adder_16_co));
endmodule

module _4_Bit_Full_Adder (
  input  a3,
  input  a2,
  input  a1,
  input  a0,
  input  b3,
  input  b2,
  input  b1,
  input  b0,
  input  CI,
  output CO,
  output s3,
  output s2,
  output s1,
  output s0
);

  wire n1_bit_full_adder_2_co, n1_bit_full_adder_3_co, n1_bit_full_adder_4_co;

  _1_Bit_Full_Adder u_1_bit_full_adder_1 (.A(a3), .B(b3), .Sum(s3), .CI(n1_bit_full_adder_3_co), .CO(CO));
  _1_Bit_Full_Adder u_1_bit_full_adder_2 (
    .A(a1), .B(b1), .Sum(s1), .CI(n1_bit_full_adder_4_co), .CO(n1_bit_full_adder_2_co));
  _1_Bit_Full_Adder u_1_bit_full_adder_3 (
    .A(a2), .B(b2), .Sum(s2), .CI(n1_bit_full_adder_2_co), .CO(n1_bit_full_adder_3_co));
  _1_Bit_Full_Adder u_1_bit_full_adder_4 (.A(a0), .B(b0), .Sum(s0), .CI(CI), .CO(n1_bit_full_adder_4_co));
endmodule

module _16_Bit_Adder_with_4_Bit_Adder (
  input  in_1,
  input  in_2,
  input  in_3,
  input  in_4,
  input  in_5,
  input  in_6,
  input  in_7,
  input  in_8,
  input  in_9,
  input  in_10,
  input  in_11,
  input  in_12,
  input  in_13,
  input  in_14,
  input  in_15,
  input  in_16,
  input  in_17,
  input  in_18,
  input  in_19,
  input  in_20,
  input  in_21,
  input  in_22,
  input  in_23,
  input  in_24,
  input  in_25,
  input  in_26,
  input  in_27,
  input  in_28,
  input  in_29,
  input  in_30,
  input  in_31,
  input  in_32,
  output out_33,
  output out_34,
  output out_35,
  output out_36,
  output out_37,
  output out_38,
  output out_39,
  output out_40,
  output out_41,
  output out_42,
  output out_43,
  output out_44,
  output out_45,
  output out_46,
  output out_47,
  output out_48,
  output out_49
);

  wire n4_bit_full_adder_2_co, n4_bit_full_adder_3_co, n4_bit_full_adder_4_co;

  _4_Bit_Full_Adder u_4_bit_full_adder_1 (
    .a3(in_1), .a2(in_2), .a1(in_3), .a0(in_4), .b3(in_17), .b2(in_18), .b1(in_19), .b0(in_20),
    .CI(n4_bit_full_adder_2_co), .CO(out_33), .s3(out_34), .s2(out_35), .s1(out_36), .s0(out_37));
  _4_Bit_Full_Adder u_4_bit_full_adder_2 (
    .a3(in_5), .a2(in_6), .a1(in_7), .a0(in_8), .b3(in_21), .b2(in_22), .b1(in_23), .b0(in_24),
    .CI(n4_bit_full_adder_3_co), .CO(n4_bit_full_adder_2_co), .s3(out_38), .s2(out_39), .s1(out_40),
    .s0(out_41));
  _4_Bit_Full_Adder u_4_bit_full_adder_3 (
    .a3(in_9), .a2(in_10), .a1(in_11), .a0(in_12), .b3(in_25), .b2(in_26), .b1(in_27), .b0(in_28),
    .CI(n4_bit_full_adder_4_co), .CO(n4_bit_full_adder_3_co), .s3(out_42), .s2(out_43), .s1(out_44),
    .s0(out_45));
  _4_Bit_Full_Adder u_4_bit_full_adder_4 (
    .a3(in_13), .a2(in_14), .a1(in_15), .a0(in_16), .b3(in_29), .b2(in_30), .b1(in_31), .b0(in_32),
    .CI(1'b0), .CO(n4_bit_full_adder_4_co), .s3(out_46), .s2(out_47), .s1(out_48), .s0(out_49));
endmodule

module _4_Bit_CLA___Deprecated (
  input  a3,
  input  a2,
  input  a1,
  input  a0,
  input  b3,
  input  b2,
  input  b1,
  input  b0,
  input  CI,
  output s3,
  output s2,
  output s1,
  output s0,
  output G,
  output P
);

  wire and_1_out, and_2_out, and_3_out, and_4_out, and_6_out, and_7_out, and_8_out, g0_out, g1_out, g2_out,
       g3_out, or_2_out, or_3_out, or_4_out, or_5_out, p0_out, p1_out, p2_out, p3_out, xor_1_out, xor_3_out,
       xor_5_out, xor_7_out;

  and g3 (g3_out, b3, a3);
  or or_1 (G, g3_out, and_3_out, and_4_out, and_1_out);
  and and_1 (and_1_out, p3_out, p2_out, p1_out, g0_out);
  or p3 (p3_out, b3, a3);
  and and_2 (and_2_out, p3_out, or_3_out);
  or or_2 (or_2_out, g3_out, and_2_out);
  xor xor_1 (xor_1_out, or_2_out, or_3_out);
  xor xor_2 (s3, xor_1_out, p3_out);
  and and_3 (and_3_out, p3_out, g2_out);
  and and_4 (and_4_out, p3_out, p2_out, g1_out);
  and g2 (g2_out, b2, a2);
  or or_3 (or_3_out, g2_out, and_6_out);
  and and_5 (P, p3_out, p2_out, p1_out, p0_out);
  or p2 (p2_out, b2, a2);
  and and_6 (and_6_out, p2_out, or_4_out);
  xor xor_3 (xor_3_out, g2_out, or_4_out);
  xor xor_4 (s2, xor_3_out, p2_out);
  or p1 (p1_out, b1, a1);
  and and_7 (and_7_out, p1_out, or_5_out);
  and g1 (g1_out, b1, a1);
  or or_4 (or_4_out, g1_out, and_7_out);
  xor xor_5 (xor_5_out, g1_out, or_5_out);
  xor xor_6 (s1, xor_5_out, p1_out);
  and g0 (g0_out, b0, a0);
  or p0 (p0_out, b0, a0);
  and and_8 (and_8_out, p0_out, CI);
  or or_5 (or_5_out, g0_out, and_8_out);
  xor xor_7 (xor_7_out, g0_out, CI);
  xor xor_8 (s0, xor_7_out, p0_out);
endmodule

module _16_Bit_Adder_with_4_Bit_CLA___Deprecated (
  input  [15:0] in_1,
  input  [15:0] in_2,
  output [15:0] out_3,
  output overflow
);

  wire n4_bit_cla_deprecated_2_g, n4_bit_cla_deprecated_3_g, n4_bit_cla_deprecated_4_g;

  _4_Bit_CLA___Deprecated u_4_bit_cla_deprecated_1 (
    .a3(in_1[15]), .a2(in_1[14]), .a1(in_1[13]), .a0(in_1[12]), .b3(in_2[15]), .b2(in_2[14]), .b1(in_2[13]),
    .b0(in_2[12]), .s0(out_3[12]), .CI(n4_bit_cla_deprecated_2_g), .G(overflow), .s1(out_3[13]),
    .s2(out_3[14]), .s3(out_3[15]));  // open: P
  // Probe on in_1
  // Probe on in_2
  _4_Bit_CLA___Deprecated u_4_bit_cla_deprecated_2 (
    .a3(in_1[11]), .a2(in_1[10]), .a1(in_1[9]), .a0(in_1[8]), .b3(in_2[11]), .b2(in_2[10]), .b1(in_2[9]),
    .b0(in_2[8]), .s0(out_3[8]), .CI(n4_bit_cla_deprecated_3_g), .G(n4_bit_cla_deprecated_2_g),
    .s1(out_3[9]), .s2(out_3[10]), .s3(out_3[11]));  // open: P
  _4_Bit_CLA___Deprecated u_4_bit_cla_deprecated_3 (
    .a3(in_1[7]), .a2(in_1[6]), .a1(in_1[5]), .a0(in_1[4]), .b3(in_2[7]), .b2(in_2[6]), .b1(in_2[5]),
    .b0(in_2[4]), .s0(out_3[4]), .CI(n4_bit_cla_deprecated_4_g), .G(n4_bit_cla_deprecated_3_g),
    .s1(out_3[5]), .s2(out_3[6]), .s3(out_3[7]));  // open: P
  // Probe on out_3
  _4_Bit_CLA___Deprecated u_4_bit_cla_deprecated_4 (
    .a3(in_1[3]), .a2(in_1[2]), .a1(in_1[1]), .a0(in_1[0]), .b3(in_2[3]), .b2(in_2[2]), .b1(in_2[1]),
    .b0(in_2[0]), .s0(out_3[0]), .CI(1'b0), .G(n4_bit_cla_deprecated_4_g), .s1(out_3[1]), .s2(out_3[2]),
    .s3(out_3[3]));  // open: P
endmodule

module _16_Bit_Full_Adder_Backup (
  input  in_1,
  input  in_2,
  input  in_3,
  input  in_4,
  input  in_5,
  input  in_6,
  input  in_7,
  input  in_8,
  input  in_9,
  input  in_10,
  input  in_11,
  input  in_12,
  input  in_13,
  input  in_14,
  input  in_15,
  input  in_16,
  input  in_17,
  input  in_18,
  input  in_19,
  input  in_20,
  input  in_21,
  input  in_22,
  input  in_23,
  input  in_24,
  input  in_25,
  input  in_26,
  input  in_27,
  input  in_28,
  input  in_29,
  input  in_30,
  input  in_31,
  input  in_32,
  output out_33,
  output out_34,
  output out_35,
  output out_36,
  output out_37,
  output out_38,
  output out_39,
  output out_40,
  output out_41,
  output out_42,
  output out_43,
  output out_44,
  output out_45,
  output out_46,
  output out_47,
  output out_48,
  output out_49
);

  wire n1_bit_full_adder_2_co, n1_bit_full_adder_3_co, n1_bit_full_adder_4_co, n1_bit_full_adder_5_co,
       n1_bit_full_adder_6_co, n1_bit_full_adder_7_co, n1_bit_full_adder_8_co, n1_bit_full_adder_9_co,
       n1_bit_full_adder_10_co, n1_bit_full_adder_11_co, n1_bit_full_adder_12_co, n1_bit_full_adder_13_co,
       n1_bit_full_adder_14_co, n1_bit_full_adder_15_co, n1_bit_full_adder_16_co;

  _1_Bit_Full_Adder u_1_bit_full_adder_1 (.A(in_1), .B(in_17), .Sum(out_34), .CI(n1_bit_full_adder_2_co), .CO(out_33));
  _1_Bit_Full_Adder u_1_bit_full_adder_2 (
    .A(in_2), .B(in_18), .Sum(out_35), .CI(n1_bit_full_adder_3_co), .CO(n1_bit_full_adder_2_co));
  _1_Bit_Full_Adder u_1_bit_full_adder_3 (
    .A(in_3), .B(in_19), .Sum(out_36), .CI(n1_bit_full_adder_4_co), .CO(n1_bit_full_adder_3_co));
  _1_Bit_Full_Adder u_1_bit_full_adder_4 (
    .A(in_4), .B(in_20), .Sum(out_37), .CI(n1_bit_full_adder_5_co), .CO(n1_bit_full_adder_4_co));
  _1_Bit_Full_Adder u_1_bit_full_adder_5 (
    .A(in_5), .B(in_21), .Sum(out_38), .CI(n1_bit_full_adder_7_co), .CO(n1_bit_full_adder_5_co));
  _1_Bit_Full_Adder u_1_bit_full_adder_6 (
    .A(in_7), .B(in_23), .Sum(out_40), .CI(n1_bit_full_adder_8_co), .CO(n1_bit_full_adder_6_co));
  _1_Bit_Full_Adder u_1_bit_full_adder_7 (
    .A(in_6), .B(in_22), .Sum(out_39), .CI(n1_bit_full_adder_6_co), .CO(n1_bit_full_adder_7_co));
  _1_Bit_Full_Adder u_1_bit_full_adder_8 (
    .A(in_8), .B(in_24), .Sum(out_41), .CI(n1_bit_full_adder_9_co), .CO(n1_bit_full_adder_8_co));
  _1_Bit_Full_Adder u_1_bit_full_adder_9 (
    .A(in_9), .B(in_25), .Sum(out_42), .CI(n1_bit_full_adder_10_co), .CO(n1_bit_full_adder_9_co));
  _1_Bit_Full_Adder u_1_bit_full_adder_10 (
    .A(in_10), .B(in_26), .Sum(out_43), .CI(n1_bit_full_adder_11_co), .CO(n1_bit_full_adder_10_co));
  _1_Bit_Full_Adder u_1_bit_full_adder_11 (
    .A(in_11), .B(in_27), .Sum(out_44), .CI(n1_bit_full_adder_12_co), .CO(n1_bit_full_adder_11_co));
  _1_Bit_Full_Adder u_1_bit_full_adder_12 (
    .A(in_12), .B(in_28), .Sum(out_45), .CI(n1_bit_full_adder_13_co), .CO(n1_bit_full_adder_12_co));
  _1_Bit_Full_Adder u_1_bit_full_adder_13 (
    .A(in_13), .B(in_29), .Sum(out_46), .CI(n1_bit_full_adder_14_co), .CO(n1_bit_full_adder_13_co));
  _1_Bit_Full_Adder u_1_bit_full_adder_14 (
    .A(in_14), .B(in_30), .Sum(out_47), .CI(n1_bit_full_adder_15_co), .CO(n1_bit_full_adder_14_co));
  _1_Bit_Full_Adder u_1_bit_full_adder_15 (
    .A(in_15), .B(in_31), .Sum(out_48), .CI(n1_bit_full_adder_16_co), .CO(n1_bit_full_adder_15_co));
  _1_Bit_Full_Adder u_1_bit_full_adder_16 (.A(in_16), .B(in_32), .Sum(out_49), .CI(1'b0), .CO(n1_bit_full_adder_16_co));
endmodule

module _4_Bit_CLA (
  input  CI,
  input  [3:0] a0,
  input  [3:0] b0,
  output [3:0] out_4,
  output P0,
  output G0
);

  wire c1_out, c2_out, c3_out, g0_out, g1_out, g2_out, g3_out, p0_c0_out, p0_out, p1_g0_out, p1_out,
       p1_p_c0_out, p2_g1_out, p2_out, p2_p1_g0_out, p2_p1_p0_c0_out, p3_g2_out, p3_out, p3_p2_g1_out,
       p3_p2_p1_g0_out;

  and u_g0 (g0_out, a0[0], b0[0]);
  or u_p0 (p0_out, a0[0], b0[0]);
  and g1 (g1_out, a0[1], b0[1]);
  or p1 (p1_out, a0[1], b0[1]);
  and g2 (g2_out, a0[2], b0[2]);
  or p2 (p2_out, a0[2], b0[2]);
  and g3 (g3_out, a0[3], b0[3]);
  or p3 (p3_out, a0[3], b0[3]);
  and p0_c0 (p0_c0_out, p0_out, CI);
  and p1_g0 (p1_g0_out, g0_out, p1_out);
  and p1_p_c0 (p1_p_c0_out, p1_out, p0_out, CI);
  and p2_g1 (p2_g1_out, g1_out, p2_out);
  and p2_p1_g0 (p2_p1_g0_out, p2_out, p1_out, g0_out);
  and p2_p1_p0_c0 (p2_p1_p0_c0_out, p2_out, p1_out, p0_out, CI);
  and p3_g2 (p3_g2_out, p3_out, g2_out);
  and p3_p2_g1 (p3_p2_g1_out, p3_out, p2_out, g1_out);
  and p3_p2_p1_g0 (p3_p2_p1_g0_out, p3_out, g2_out, g1_out, g0_out);
  or c1 (c1_out, g0_out, p0_c0_out);
  or c2 (c2_out, g1_out, p1_g0_out, p1_p_c0_out);
  or c3 (c3_out, g2_out, p2_g1_out, p2_p1_g0_out, p2_p1_p0_c0_out);
  or P0_2 (P0, g0_out, p1_out, p2_out, g3_out);
  or G0_2 (G0, g3_out, p3_g2_out, p3_p2_g1_out, p3_p2_p1_g0_out);
  _1_Bit_Full_Adder_without_CO u_1_bit_full_adder_without_co_1 (.A(a0[0]), .B(b0[0]), .CI(CI), .Sum(out_4[0]));
  _1_Bit_Full_Adder_without_CO u_1_bit_full_adder_without_co_2 (.A(a0[1]), .B(b0[1]), .CI(c1_out), .Sum(out_4[1]));
  _1_Bit_Full_Adder_without_CO u_1_bit_full_adder_without_co_3 (.A(a0[2]), .B(b0[2]), .CI(c2_out), .Sum(out_4[2]));
  _1_Bit_Full_Adder_without_CO u_1_bit_full_adder_without_co_4 (.A(a0[3]), .B(b0[3]), .CI(c3_out), .Sum(out_4[3]));
endmodule

module _4_Bit_CLA_Optimised (
  input  CI,
  input  [3:0] in_2,
  input  [3:0] in_3,
  output G0,
  output P0,
  output Overflow,
  output [3:0] out_7
);

  wire and_1_out, and_2_out, and_3_out, and_4_out, carry_lookahead_unit_1_c1, carry_lookahead_unit_1_c2,
       carry_lookahead_unit_1_c3, carry_lookahead_unit_1_c4, or_1_out, or_2_out, or_3_out, or_4_out;

  _1_Bit_Full_Adder_without_CO u_1_bit_full_adder_without_co_1 (
    .A(in_3[3]), .B(in_2[3]), .CI(carry_lookahead_unit_1_c3), .Sum(out_7[3]));
  _1_Bit_Full_Adder_without_CO u_1_bit_full_adder_without_co_2 (
    .A(in_3[2]), .B(in_2[2]), .CI(carry_lookahead_unit_1_c2), .Sum(out_7[2]));
  _1_Bit_Full_Adder_without_CO u_1_bit_full_adder_without_co_3 (
    .A(in_3[1]), .B(in_2[1]), .CI(carry_lookahead_unit_1_c1), .Sum(out_7[1]));
  _1_Bit_Full_Adder_without_CO u_1_bit_full_adder_without_co_4 (.A(in_2[0]), .B(in_3[0]), .CI(CI), .Sum(out_7[0]));
  and and_1 (and_1_out, in_2[3], in_3[3]);
  or or_1 (or_1_out, in_2[3], in_3[3]);
  and and_2 (and_2_out, in_2[2], in_3[2]);
  or or_2 (or_2_out, in_2[2], in_3[2]);
  Carry_lookahead_unit carry_lookahead_unit_1 (
    .g0(and_4_out), .p0(or_4_out), .g1(and_3_out), .p1(or_3_out), .g2(and_2_out), .p2(or_2_out),
    .g3(and_1_out), .p3(or_1_out), .c1(carry_lookahead_unit_1_c1), .c2(carry_lookahead_unit_1_c2),
    .c3(carry_lookahead_unit_1_c3), .c4(carry_lookahead_unit_1_c4), .P0_2(P0), .G0_2(G0), .CI(CI));
  and and_3 (and_3_out, in_2[1], in_3[1]);
  or or_3 (or_3_out, in_2[1], in_3[1]);
  and and_4 (and_4_out, in_2[0], in_3[0]);
  or or_4 (or_4_out, in_2[0], in_3[0]);
  xor xor_1 (Overflow, carry_lookahead_unit_1_c3, carry_lookahead_unit_1_c4);
endmodule

module _1_Bit_Full_Adder_without_CO (
  input  CI,
  input  A,
  input  B,
  output Sum
);

  wire xor_1_out;

  xor xor_1 (xor_1_out, A, B);
  xor xor_2 (Sum, CI, xor_1_out);
endmodule

module Carry_lookahead_unit (
  input  CI,
  input  g0,
  input  p0,
  input  g1,
  input  p1,
  input  g2,
  input  p2,
  input  g3,
  input  p3,
  output c1,
  output c2,
  output c3,
  output c4,
  output P0_2,
  output G0_2
);

  wire p0_c0_out, p1_g0_out, p1_p_c0_out, p2_g1_out, p2_p1_g0_out, p2_p1_p0_c0_out, p3_g2_2_out, p3_g2_out,
       p3_p2_g1_2_out, p3_p2_g1_out, p3_p2_p1_g0_2_out, p3_p2_p1_g0_out, p3_p2_p1_p0_c0_out;

  and p0_c0 (p0_c0_out, p0, CI);
  and p1_g0 (p1_g0_out, g0, p1);
  and p1_p_c0 (p1_p_c0_out, p1, p0, CI);
  and p2_g1 (p2_g1_out, g1, p2);
  and p2_p1_g0 (p2_p1_g0_out, p2, p1, g0);
  and p2_p1_p0_c0 (p2_p1_p0_c0_out, p2, p1, p0, CI);
  and p3_g2 (p3_g2_out, g2, p3);
  and p3_p2_g1 (p3_p2_g1_out, p3, p2, g1);
  and p3_p2_p1_g0 (p3_p2_p1_g0_out, p3, p2, p1, g0);
  and p3_p2_p1_p0_c0 (p3_p2_p1_p0_c0_out, p3, p2, p1, p0, CI);
  and p3_g2_2 (p3_g2_2_out, p3, g2);
  and p3_p2_g1_2 (p3_p2_g1_2_out, p3, p2, g1);
  and p3_p2_p1_g0_2 (p3_p2_p1_g0_2_out, p3, p2, p1, g0);
  or u_c1 (c1, g0, p0_c0_out);
  or u_c2 (c2, g1, p1_g0_out, p1_p_c0_out);
  or u_c3 (c3, g2, p2_g1_out, p2_p1_g0_out, p2_p1_p0_c0_out);
  or u_c4 (c4, g3, p3_g2_out, p3_p2_g1_out, p3_p2_p1_g0_out, p3_p2_p1_p0_c0_out);
  and u_P0 (P0_2, p0, p1, p2, p3);
  or u_G0 (G0_2, g3, p3_g2_2_out, p3_p2_g1_2_out, p3_p2_p1_g0_2_out);
endmodule

module _16_Bit_CLA_Optimised (
  input  [15:0] in_1,
  input  [15:0] in_2,
  output C4,
  output Overflow,
  output [15:0] out_5
);

  wire carry_lookahead_unit_1_c1, carry_lookahead_unit_1_c2, carry_lookahead_unit_1_c3,
       n4_bit_cla_optimised_1_g0, n4_bit_cla_optimised_1_p0, n4_bit_cla_optimised_2_g0,
       n4_bit_cla_optimised_2_p0, n4_bit_cla_optimised_3_g0, n4_bit_cla_optimised_3_p0,
       n4_bit_cla_optimised_4_g0, n4_bit_cla_optimised_4_p0;

  // Probe on in_1
  _4_Bit_CLA_Optimised u_4_bit_cla_optimised_1 (
    .in_2(in_2[15:12]), .in_3(in_1[15:12]), .G0(n4_bit_cla_optimised_1_g0), .P0(n4_bit_cla_optimised_1_p0),
    .out_7(out_5[15:12]), .CI(carry_lookahead_unit_1_c3), .Overflow(Overflow));
  _4_Bit_CLA_Optimised u_4_bit_cla_optimised_2 (
    .in_2(in_2[11:8]), .in_3(in_1[11:8]), .G0(n4_bit_cla_optimised_2_g0), .P0(n4_bit_cla_optimised_2_p0),
    .out_7(out_5[11:8]), .CI(carry_lookahead_unit_1_c2));  // open: Overflow
  // Probe on out_5
  Carry_lookahead_unit carry_lookahead_unit_1 (
    .g0(n4_bit_cla_optimised_4_g0), .p0(n4_bit_cla_optimised_4_p0), .g1(n4_bit_cla_optimised_3_g0),
    .p1(n4_bit_cla_optimised_3_p0), .g2(n4_bit_cla_optimised_2_g0), .p2(n4_bit_cla_optimised_2_p0),
    .g3(n4_bit_cla_optimised_1_g0), .p3(n4_bit_cla_optimised_1_p0), .c1(carry_lookahead_unit_1_c1),
    .c2(carry_lookahead_unit_1_c2), .c3(carry_lookahead_unit_1_c3), .c4(C4), .CI(1'b0));  // open: P0_2, G0_2
  _4_Bit_CLA_Optimised u_4_bit_cla_optimised_3 (
    .in_2(in_2[7:4]), .in_3(in_1[7:4]), .G0(n4_bit_cla_optimised_3_g0), .P0(n4_bit_cla_optimised_3_p0),
    .out_7(out_5[7:4]), .CI(carry_lookahead_unit_1_c1));  // open: Overflow
  _4_Bit_CLA_Optimised u_4_bit_cla_optimised_4 (
    .in_2(in_2[3:0]), .in_3(in_1[3:0]), .G0(n4_bit_cla_optimised_4_g0), .P0(n4_bit_cla_optimised_4_p0),
    .out_7(out_5[3:0]), .CI(1'b0));  // open: Overflow
  // Probe on in_2
endmodule

module Compare (
  input  [15:0] in_1,
  input  [15:0] in_2,
  output [15:0] out_3,
  output [15:0] out_4
);

  // Probe on in_1
  // Probe on in_2
  _16_Bit_ripple_adder u_16_bit_ripple_adder_1 (.in_1(in_1), .in_2(in_2), .out_4(out_3));  // open: out_3
  _16_Bit_CLA_Optimised u_16_bit_cla_optimised_1 (.in_1(in_1), .in_2(in_2), .out_5(out_4));  // open: Overflow, C4
  // Probe on out_3
  // Probe on out_4
endmodule

module _16_Bit_ripple_adder (
  input  [15:0] in_1,
  input  [15:0] in_2,
  output out_3,
  output [15:0] out_4
);

  wire n4_bit_full_adder_2_co, n4_bit_full_adder_3_co, n4_bit_full_adder_4_co;

  _4_Bit_Full_Adder u_4_bit_full_adder_1 (
    .a3(in_2[15]), .a2(in_2[14]), .a1(in_2[13]), .a0(in_2[12]), .b3(in_1[15]), .b2(in_1[14]), .b1(in_1[13]),
    .b0(in_1[12]), .CI(n4_bit_full_adder_2_co), .CO(out_3), .s3(out_4[15]), .s2(out_4[14]), .s1(out_4[13]),
    .s0(out_4[12]));
  _4_Bit_Full_Adder u_4_bit_full_adder_2 (
    .a3(in_2[11]), .a2(in_2[10]), .a1(in_2[9]), .a0(in_2[8]), .b3(in_1[11]), .b2(in_1[10]), .b1(in_1[9]),
    .b0(in_1[8]), .CI(n4_bit_full_adder_3_co), .CO(n4_bit_full_adder_2_co), .s3(out_4[11]), .s2(out_4[10]),
    .s1(out_4[9]), .s0(out_4[8]));
  _4_Bit_Full_Adder u_4_bit_full_adder_3 (
    .a3(in_2[7]), .a2(in_2[6]), .a1(in_2[5]), .a0(in_2[4]), .b3(in_1[7]), .b2(in_1[6]), .b1(in_1[5]),
    .b0(in_1[4]), .CI(n4_bit_full_adder_4_co), .CO(n4_bit_full_adder_3_co), .s3(out_4[7]), .s2(out_4[6]),
    .s1(out_4[5]), .s0(out_4[4]));
  _4_Bit_Full_Adder u_4_bit_full_adder_4 (
    .a3(in_2[3]), .a2(in_2[2]), .a1(in_2[1]), .a0(in_2[0]), .b3(in_1[3]), .b2(in_1[2]), .b1(in_1[1]),
    .b0(in_1[0]), .CI(1'b0), .CO(n4_bit_full_adder_4_co), .s3(out_4[3]), .s2(out_4[2]), .s1(out_4[1]),
    .s0(out_4[0]));
endmodule
